// Logisim project project.circ as structural Verilog
module Main (
  input  initgame,
  input  clk,
  input  [6:0] moving,
  output [31:0] out_4,
  output [31:0] out_5,
  output [31:0] out_6,
  output [31:0] out_7,
  output [31:0] out_8,
  output [31:0] out_9,
  output [31:0] out_10,
  output [31:0] out_11,
  output [31:0] out_12,
  output [31:0] out_13,
  output [31:0] out_14,
  output [31:0] out_15,
  output [31:0] out_16,
  output [31:0] out_17,
  output [31:0] out_18,
  output [31:0] out_19,
  output [31:0] out_20,
  output [31:0] out_21,
  output [31:0] out_22,
  output [31:0] out_23,
  output [31:0] out_24,
  output [31:0] out_25,
  output [31:0] out_26,
  output [31:0] out_27,
  output [31:0] out_28,
  output [31:0] out_29,
  output [31:0] out_30,
  output [31:0] out_31,
  output [31:0] out_32,
  output [31:0] out_33,
  output [31:0] out_34,
  output [31:0] out_35,
  output gameover,
  output win
);

  wire comparator_1_eq, comparator_2_eq, comparator_3_eq, enemies_1_boom, or32_1_out, or32_2_out, or32_3_out,
       or_2_out, walls_1_out_5, walls_1_out_6;
  wire [4:0] plcoord, \shooting_1_номер ;
  wire [31:0] _0_prime_prime, _1_prime, _1_prime_prime, _2_prime, _3_prime, _4_prime, _5_prime,
       _5_prime_prime, _6_prime, _7_prime, _8_prime, _9_prime, _10_prime, _11_prime, _12_prime, _13_prime,
       _14_prime, _15_prime, _16_prime, _17_prime, _18_prime, _19_prime, _20_prime, _21_prime, _22_prime,
       _23_prime, _24_prime, _25_prime, _26_prime, _27_prime, _28_prime, _29_prime, _30_prime, _31_prime,
       _32_prime, and_1_out, and_2_out, enemies_1_out_43, shooting_1__2, shooting_1__3, shooting_1__31,
       shooting_1_out_6, shooting_1_out_7, shooting_1_out_8, shooting_1_out_9, shooting_1_out_11,
       shooting_1_out_12, shooting_1_out_13, shooting_1_out_14, shooting_1_out_16, shooting_1_out_17,
       shooting_1_out_18, shooting_1_out_19, shooting_1_out_20, shooting_1_out_21, shooting_1_out_22,
       shooting_1_out_23, shooting_1_out_24, shooting_1_out_26, shooting_1_out_27, shooting_1_out_28,
       shooting_1_out_29, shooting_1_out_30, shooting_1_out_31, shooting_1_out_32, shooting_1_out_33,
       shooting_1_out_34, wall;

  Comparator #(.width(7), .mode("unsigned")) comparator_1 (
    .a(moving), .b(7'b1100001), .eq(comparator_1_eq));  // open: gt, lt
  Or32 or32_1 (.in(and_1_out), .out(or32_1_out));
  assign and_1_out = _0_prime_prime & _1_prime;  // AND_Gate and_1, 32 bits wide
  Or32 or32_2 (.in(enemies_1_out_43), .out(or32_2_out));
  assign and_2_out = _1_prime_prime & _2_prime;  // AND_Gate and_2, 32 bits wide
  Or32 or32_3 (.in(and_2_out), .out(or32_3_out));
  Walls walls_1 (
    .clk(clk), .bull_2(_5_prime_prime), .wall(wall), .init(initgame), .out_6(walls_1_out_6), .bull(_4_prime),
    .out_5(walls_1_out_5));
  Player_Move player_move_1 (
    .counter(plcoord), .l(comparator_1_eq), .r(comparator_2_eq), ._0(_0_prime_prime), ._1(_1_prime_prime));
  Comparator #(.width(7), .mode("unsigned")) comparator_2 (
    .a(moving), .b(7'b1100100), .eq(comparator_2_eq));  // open: gt, lt
  Comparator #(.width(7), .mode("unsigned")) comparator_3 (
    .a(moving), .b(7'b0100000), .eq(comparator_3_eq));  // open: gt, lt
  or or_1 (gameover, or32_1_out, or32_2_out, or32_3_out);
  or or_2 (or_2_out, enemies_1_boom, walls_1_out_6);
  Shooting shooting_1 (
    ._2(shooting_1__2), ._3(shooting_1__3), .out_15(_5_prime_prime), .coord(plcoord),
    .out_20(shooting_1_out_20), .out_26(shooting_1_out_26), .out_31(shooting_1_out_31),
    .fire(comparator_3_eq), .out_6(shooting_1_out_6), .out_11(shooting_1_out_11), .out_16(shooting_1_out_16),
    .out_21(shooting_1_out_21), .out_27(shooting_1_out_27), .out_32(shooting_1_out_32),
    .out_7(shooting_1_out_7), .out_12(shooting_1_out_12), .out_17(shooting_1_out_17),
    .out_22(shooting_1_out_22), .out_28(shooting_1_out_28), .out_33(shooting_1_out_33),
    .out_8(shooting_1_out_8), .out_13(shooting_1_out_13), .out_18(shooting_1_out_18),
    .out_23(shooting_1_out_23), .out_29(shooting_1_out_29), .out_34(shooting_1_out_34),
    .out_9(shooting_1_out_9), .out_14(shooting_1_out_14), .out_19(shooting_1_out_19),
    .out_24(shooting_1_out_24), .out_30(shooting_1_out_30), ._31(shooting_1__31), .clk(clk),
    .\Номер (\shooting_1_номер ), .reset(or_2_out));
  assign out_35 = _32_prime | shooting_1__31;  // OR_Gate or_3, 32 bits wide
  assign out_31 = _31_prime | shooting_1_out_30;  // OR_Gate or_4, 32 bits wide
  assign out_27 = _30_prime | shooting_1_out_24;  // OR_Gate or_5, 32 bits wide
  assign out_23 = _29_prime | shooting_1_out_19;  // OR_Gate or_6, 32 bits wide
  assign out_19 = _28_prime | shooting_1_out_14;  // OR_Gate or_7, 32 bits wide
  assign out_15 = _27_prime | shooting_1_out_9;  // OR_Gate or_8, 32 bits wide
  assign out_11 = _26_prime | shooting_1_out_34;  // OR_Gate or_9, 32 bits wide
  assign out_7 = _25_prime | shooting_1_out_29;  // OR_Gate or_10, 32 bits wide
  assign out_34 = _24_prime | shooting_1_out_23;  // OR_Gate or_11, 32 bits wide
  assign out_30 = _23_prime | shooting_1_out_18;  // OR_Gate or_12, 32 bits wide
  assign out_26 = _22_prime | shooting_1_out_13;  // OR_Gate or_13, 32 bits wide
  assign out_22 = _21_prime | shooting_1_out_8;  // OR_Gate or_14, 32 bits wide
  assign out_18 = _20_prime | shooting_1_out_33;  // OR_Gate or_15, 32 bits wide
  assign out_14 = _19_prime | shooting_1_out_28;  // OR_Gate or_16, 32 bits wide
  assign out_10 = _18_prime | shooting_1_out_22;  // OR_Gate or_17, 32 bits wide
  assign out_6 = _17_prime | shooting_1_out_17;  // OR_Gate or_18, 32 bits wide
  assign out_33 = _16_prime | shooting_1_out_12;  // OR_Gate or_19, 32 bits wide
  assign out_29 = _15_prime | shooting_1_out_7;  // OR_Gate or_20, 32 bits wide
  assign out_25 = _14_prime | shooting_1_out_32;  // OR_Gate or_21, 32 bits wide
  assign out_21 = _13_prime | shooting_1_out_27;  // OR_Gate or_22, 32 bits wide
  assign out_17 = _12_prime | shooting_1_out_21;  // OR_Gate or_23, 32 bits wide
  assign out_13 = _11_prime | shooting_1_out_16;  // OR_Gate or_24, 32 bits wide
  assign out_9 = _10_prime | shooting_1_out_11;  // OR_Gate or_25, 32 bits wide
  assign out_5 = _9_prime | shooting_1_out_6;  // OR_Gate or_26, 32 bits wide
  assign out_32 = shooting_1_out_31 | _8_prime;  // OR_Gate or_27, 32 bits wide
  assign out_28 = shooting_1_out_26 | _7_prime;  // OR_Gate or_28, 32 bits wide
  assign out_24 = shooting_1_out_20 | _6_prime;  // OR_Gate or_29, 32 bits wide
  assign out_20 = _5_prime_prime | _5_prime;  // OR_Gate or_30, 32 bits wide
  assign out_16 = wall | _4_prime | shooting_1__3;  // OR_Gate or_31, 32 bits wide
  assign out_12 = shooting_1__2 | _3_prime;  // OR_Gate or_32, 32 bits wide
  Enemies enemies_1 (
    .clk(clk), .boom(enemies_1_boom), .Num(\shooting_1_номер ), .in_3(shooting_1_out_33),
    .in_4(shooting_1__31), .in_6(shooting_1_out_28), .in_7(shooting_1_out_30), .in_8(shooting_1_out_22),
    .in_9(shooting_1_out_24), .in_10(shooting_1_out_17), .in_11(shooting_1_out_19),
    .in_12(shooting_1_out_12), .in_13(shooting_1_out_14), .in_14(shooting_1_out_7), .in_15(shooting_1_out_9),
    .in_18(shooting_1_out_32), .in_19(shooting_1_out_34), .in_21(shooting_1_out_27),
    .in_22(shooting_1_out_29), .in_24(shooting_1_out_21), .in_25(shooting_1_out_23),
    .in_27(shooting_1_out_16), .in_28(shooting_1_out_18), .in_30(shooting_1_out_11),
    .in_31(shooting_1_out_13), .in_32(shooting_1__2), .in_33(shooting_1_out_6), .in_34(shooting_1_out_8),
    .out_36(_20_prime), .out_37(_32_prime), .out_38(_19_prime), .out_39(_31_prime), .out_41(_18_prime),
    .out_42(_30_prime), .out_44(_17_prime), .out_45(_29_prime), .out_46(_16_prime), .out_47(_28_prime),
    .out_49(_15_prime), .out_50(_27_prime), .out_52(_14_prime), .out_53(_26_prime), .out_55(_13_prime),
    .out_56(_25_prime), .out_58(_12_prime), .out_59(_24_prime), .out_61(_11_prime), .out_62(_23_prime),
    .out_64(_10_prime), .out_65(_22_prime), .out_67(_9_prime), .out_68(_21_prime), .in_29(shooting_1__3),
    .in_26(_5_prime_prime), .in_23(shooting_1_out_20), .in_20(shooting_1_out_26), .in_17(shooting_1_out_31),
    .out_54(_3_prime), .out_57(_4_prime), .out_60(_5_prime), .out_63(_6_prime), .out_66(_7_prime),
    .out_69(_8_prime), .out_51(_2_prime), .out_48(_1_prime), .win(win), .out_43(enemies_1_out_43),
    .wall(walls_1_out_5), .initgame(initgame));
  assign out_8 = _2_prime | _1_prime_prime;  // OR_Gate or_33, 32 bits wide
  assign out_4 = _1_prime | _0_prime_prime;  // OR_Gate or_34, 32 bits wide

  // Other names for the same wires on the sheet: _0[31:0] = out_4; _1[31:0] = out_8; _2[31:0] = out_12;
  //   _3[31:0] = out_16; _4[31:0] = out_20; _5[31:0] = out_24; _6[31:0] = out_28; _7[31:0] = out_32; _8[31:0] = out_5;
  //   _9[31:0] = out_9; _10[31:0] = out_13; _11[31:0] = out_17; _12[31:0] = out_21; _13[31:0] = out_25;
  //   _14[31:0] = out_29; _15[31:0] = out_33; _16[31:0] = out_6; _17[31:0] = out_10; _18[31:0] = out_14;
  //   _19[31:0] = out_18; _20[31:0] = out_22; _21[31:0] = out_26; _22[31:0] = out_30; _23[31:0] = out_34;
  //   _24[31:0] = out_7; _25[31:0] = out_11; _26[31:0] = out_15; _27[31:0] = out_19; _28[31:0] = out_23;
  //   _29[31:0] = out_27; _30[31:0] = out_31; _31[31:0] = out_35; init = initgame
endmodule

module Inc_5bit (
  input  [4:0] X,
  output [4:0] R,
  output Cout
);

  wire [4:1] and_1_out;

  assign {Cout, and_1_out} = {and_1_out, 1'b1} & X;  // AND_Gate and_1, 5 bits wide
  assign R = X ^ {and_1_out, 1'b1};  // XOR_Gate xor_1, 5 bits wide
endmodule

module Player_Move (
  input  l,
  input  r,
  output [4:0] counter,
  output [31:0] _1,
  output [31:0] _0
);

  wire or_1_out;
  wire [31:0] shifter_1_out, shifter_2_out;

  or or_1 (or_1_out, l, r);
  Counter #(.width(5), .max('h1f)) counter_1 (.load(l), .Q(counter), .clk(or_1_out));  // open: D, count, carry, clr
  Decoder #(.select(5), .enable("false")) decoder_1 (
    .out0(_1[31]), .out1(_1[30]), .out2(_1[29]), .out3(_1[28]), .out4(_1[27]), .out5(_1[26]), .out6(_1[25]),
    .out7(_1[24]), .out8(_1[23]), .out9(_1[22]), .out10(_1[21]), .out11(_1[20]), .out12(_1[19]),
    .out13(_1[18]), .out14(_1[17]), .out15(_1[16]), .out16(_1[15]), .out17(_1[14]), .out18(_1[13]),
    .out19(_1[12]), .out20(_1[11]), .out21(_1[10]), .out22(_1[9]), .out23(_1[8]), .out24(_1[7]),
    .out25(_1[6]), .out26(_1[5]), .out27(_1[4]), .out28(_1[3]), .out29(_1[2]), .out30(_1[1]), .out31(_1[0]),
    .sel(counter));
  Shifter #(.width(32), .shift("lr")) shifter_1 (.in(_1), .\dist (5'b00001), .out(shifter_1_out));
  Shifter #(.width(32)) shifter_2 (.in(_1), .\dist (5'b00001), .out(shifter_2_out));
  assign _0 = shifter_2_out | _1 | shifter_1_out;  // OR_Gate or_2, 32 bits wide
endmodule

module Transpon_field (
  input  [31:0] in_1,
  input  [31:0] in_2,
  input  [31:0] in_3,
  input  [31:0] in_4,
  input  [31:0] in_5,
  input  [31:0] in_6,
  input  [31:0] in_7,
  input  [31:0] in_8,
  input  [31:0] in_9,
  input  [31:0] in_10,
  input  [31:0] in_11,
  input  [31:0] in_12,
  input  [31:0] in_13,
  input  [31:0] in_14,
  input  [31:0] in_15,
  input  [31:0] in_16,
  input  [31:0] in_17,
  input  [31:0] in_18,
  input  [31:0] in_19,
  input  [31:0] in_20,
  input  [31:0] in_21,
  input  [31:0] in_22,
  input  [31:0] in_23,
  input  [31:0] in_24,
  input  [31:0] in_25,
  input  [31:0] in_26,
  input  [31:0] in_27,
  input  [31:0] in_28,
  input  [31:0] in_29,
  input  [31:0] in_30,
  input  [31:0] in_31,
  input  [31:0] in_32,
  output [31:0] _0,
  output [31:0] _1,
  output [31:0] _2,
  output [31:0] _3,
  output [31:0] _4,
  output [31:0] _5,
  output [31:0] _6,
  output [31:0] _7,
  output [31:0] _8,
  output [31:0] _9,
  output [31:0] _10,
  output [31:0] _11,
  output [31:0] _12,
  output [31:0] _13,
  output [31:0] _14,
  output [31:0] _15,
  output [31:0] _16,
  output [31:0] _17,
  output [31:0] _18,
  output [31:0] _19,
  output [31:0] _20,
  output [31:0] _21,
  output [31:0] _22,
  output [31:0] _23,
  output [31:0] _24,
  output [31:0] _25,
  output [31:0] _26,
  output [31:0] _27,
  output [31:0] _28,
  output [31:0] _29,
  output [31:0] _30,
  output [31:0] _31
);


  assign _0 = {in_1[0], in_2[0], in_3[0], in_4[0], in_5[0], in_6[0], in_7[0], in_8[0], in_9[0], in_10[0], in_11[0], in_12[0], in_13[0], in_14[0], in_15[0], in_16[0], in_17[0], in_18[0], in_19[0], in_20[0], in_21[0], in_22[0], in_23[0], in_24[0], in_25[0], in_26[0], in_27[0], in_28[0], in_29[0], in_30[0], in_31[0], in_32[0]};
  assign _1 = {in_1[1], in_2[1], in_3[1], in_4[1], in_5[1], in_6[1], in_7[1], in_8[1], in_9[1], in_10[1], in_11[1], in_12[1], in_13[1], in_14[1], in_15[1], in_16[1], in_17[1], in_18[1], in_19[1], in_20[1], in_21[1], in_22[1], in_23[1], in_24[1], in_25[1], in_26[1], in_27[1], in_28[1], in_29[1], in_30[1], in_31[1], in_32[1]};
  assign _2 = {in_1[2], in_2[2], in_3[2], in_4[2], in_5[2], in_6[2], in_7[2], in_8[2], in_9[2], in_10[2], in_11[2], in_12[2], in_13[2], in_14[2], in_15[2], in_16[2], in_17[2], in_18[2], in_19[2], in_20[2], in_21[2], in_22[2], in_23[2], in_24[2], in_25[2], in_26[2], in_27[2], in_28[2], in_29[2], in_30[2], in_31[2], in_32[2]};
  assign _3 = {in_1[3], in_2[3], in_3[3], in_4[3], in_5[3], in_6[3], in_7[3], in_8[3], in_9[3], in_10[3], in_11[3], in_12[3], in_13[3], in_14[3], in_15[3], in_16[3], in_17[3], in_18[3], in_19[3], in_20[3], in_21[3], in_22[3], in_23[3], in_24[3], in_25[3], in_26[3], in_27[3], in_28[3], in_29[3], in_30[3], in_31[3], in_32[3]};
  assign _4 = {in_1[4], in_2[4], in_3[4], in_4[4], in_5[4], in_6[4], in_7[4], in_8[4], in_9[4], in_10[4], in_11[4], in_12[4], in_13[4], in_14[4], in_15[4], in_16[4], in_17[4], in_18[4], in_19[4], in_20[4], in_21[4], in_22[4], in_23[4], in_24[4], in_25[4], in_26[4], in_27[4], in_28[4], in_29[4], in_30[4], in_31[4], in_32[4]};
  assign _5 = {in_1[5], in_2[5], in_3[5], in_4[5], in_5[5], in_6[5], in_7[5], in_8[5], in_9[5], in_10[5], in_11[5], in_12[5], in_13[5], in_14[5], in_15[5], in_16[5], in_17[5], in_18[5], in_19[5], in_20[5], in_21[5], in_22[5], in_23[5], in_24[5], in_25[5], in_26[5], in_27[5], in_28[5], in_29[5], in_30[5], in_31[5], in_32[5]};
  assign _6 = {in_1[6], in_2[6], in_3[6], in_4[6], in_5[6], in_6[6], in_7[6], in_8[6], in_9[6], in_10[6], in_11[6], in_12[6], in_13[6], in_14[6], in_15[6], in_16[6], in_17[6], in_18[6], in_19[6], in_20[6], in_21[6], in_22[6], in_23[6], in_24[6], in_25[6], in_26[6], in_27[6], in_28[6], in_29[6], in_30[6], in_31[6], in_32[6]};
  assign _7 = {in_1[7], in_2[7], in_3[7], in_4[7], in_5[7], in_6[7], in_7[7], in_8[7], in_9[7], in_10[7], in_11[7], in_12[7], in_13[7], in_14[7], in_15[7], in_16[7], in_17[7], in_18[7], in_19[7], in_20[7], in_21[7], in_22[7], in_23[7], in_24[7], in_25[7], in_26[7], in_27[7], in_28[7], in_29[7], in_30[7], in_31[7], in_32[7]};
  assign _8 = {in_1[8], in_2[8], in_3[8], in_4[8], in_5[8], in_6[8], in_7[8], in_8[8], in_9[8], in_10[8], in_11[8], in_12[8], in_13[8], in_14[8], in_15[8], in_16[8], in_17[8], in_18[8], in_19[8], in_20[8], in_21[8], in_22[8], in_23[8], in_24[8], in_25[8], in_26[8], in_27[8], in_28[8], in_29[8], in_30[8], in_31[8], in_32[8]};
  assign _9 = {in_1[9], in_2[9], in_3[9], in_4[9], in_5[9], in_6[9], in_7[9], in_8[9], in_9[9], in_10[9], in_11[9], in_12[9], in_13[9], in_14[9], in_15[9], in_16[9], in_17[9], in_18[9], in_19[9], in_20[9], in_21[9], in_22[9], in_23[9], in_24[9], in_25[9], in_26[9], in_27[9], in_28[9], in_29[9], in_30[9], in_31[9], in_32[9]};
  assign _10 = {in_1[10], in_2[10], in_3[10], in_4[10], in_5[10], in_6[10], in_7[10], in_8[10], in_9[10], in_10[10], in_11[10], in_12[10], in_13[10], in_14[10], in_15[10], in_16[10], in_17[10], in_18[10], in_19[10], in_20[10], in_21[10], in_22[10], in_23[10], in_24[10], in_25[10], in_26[10], in_27[10], in_28[10], in_29[10], in_30[10], in_31[10], in_32[10]};
  assign _11 = {in_1[11], in_2[11], in_3[11], in_4[11], in_5[11], in_6[11], in_7[11], in_8[11], in_9[11], in_10[11], in_11[11], in_12[11], in_13[11], in_14[11], in_15[11], in_16[11], in_17[11], in_18[11], in_19[11], in_20[11], in_21[11], in_22[11], in_23[11], in_24[11], in_25[11], in_26[11], in_27[11], in_28[11], in_29[11], in_30[11], in_31[11], in_32[11]};
  assign _12 = {in_1[12], in_2[12], in_3[12], in_4[12], in_5[12], in_6[12], in_7[12], in_8[12], in_9[12], in_10[12], in_11[12], in_12[12], in_13[12], in_14[12], in_15[12], in_16[12], in_17[12], in_18[12], in_19[12], in_20[12], in_21[12], in_22[12], in_23[12], in_24[12], in_25[12], in_26[12], in_27[12], in_28[12], in_29[12], in_30[12], in_31[12], in_32[12]};
  assign _13 = {in_1[13], in_2[13], in_3[13], in_4[13], in_5[13], in_6[13], in_7[13], in_8[13], in_9[13], in_10[13], in_11[13], in_12[13], in_13[13], in_14[13], in_15[13], in_16[13], in_17[13], in_18[13], in_19[13], in_20[13], in_21[13], in_22[13], in_23[13], in_24[13], in_25[13], in_26[13], in_27[13], in_28[13], in_29[13], in_30[13], in_31[13], in_32[13]};
  assign _14 = {in_1[14], in_2[14], in_3[14], in_4[14], in_5[14], in_6[14], in_7[14], in_8[14], in_9[14], in_10[14], in_11[14], in_12[14], in_13[14], in_14[14], in_15[14], in_16[14], in_17[14], in_18[14], in_19[14], in_20[14], in_21[14], in_22[14], in_23[14], in_24[14], in_25[14], in_26[14], in_27[14], in_28[14], in_29[14], in_30[14], in_31[14], in_32[14]};
  assign _15 = {in_1[15], in_2[15], in_3[15], in_4[15], in_5[15], in_6[15], in_7[15], in_8[15], in_9[15], in_10[15], in_11[15], in_12[15], in_13[15], in_14[15], in_15[15], in_16[15], in_17[15], in_18[15], in_19[15], in_20[15], in_21[15], in_22[15], in_23[15], in_24[15], in_25[15], in_26[15], in_27[15], in_28[15], in_29[15], in_30[15], in_31[15], in_32[15]};
  assign _16 = {in_1[16], in_2[16], in_3[16], in_4[16], in_5[16], in_6[16], in_7[16], in_8[16], in_9[16], in_10[16], in_11[16], in_12[16], in_13[16], in_14[16], in_15[16], in_16[16], in_17[16], in_18[16], in_19[16], in_20[16], in_21[16], in_22[16], in_23[16], in_24[16], in_25[16], in_26[16], in_27[16], in_28[16], in_29[16], in_30[16], in_31[16], in_32[16]};
  assign _17 = {in_1[17], in_2[17], in_3[17], in_4[17], in_5[17], in_6[17], in_7[17], in_8[17], in_9[17], in_10[17], in_11[17], in_12[17], in_13[17], in_14[17], in_15[17], in_16[17], in_17[17], in_18[17], in_19[17], in_20[17], in_21[17], in_22[17], in_23[17], in_24[17], in_25[17], in_26[17], in_27[17], in_28[17], in_29[17], in_30[17], in_31[17], in_32[17]};
  assign _18 = {in_1[18], in_2[18], in_3[18], in_4[18], in_5[18], in_6[18], in_7[18], in_8[18], in_9[18], in_10[18], in_11[18], in_12[18], in_13[18], in_14[18], in_15[18], in_16[18], in_17[18], in_18[18], in_19[18], in_20[18], in_21[18], in_22[18], in_23[18], in_24[18], in_25[18], in_26[18], in_27[18], in_28[18], in_29[18], in_30[18], in_31[18], in_32[18]};
  assign _19 = {in_1[19], in_2[19], in_3[19], in_4[19], in_5[19], in_6[19], in_7[19], in_8[19], in_9[19], in_10[19], in_11[19], in_12[19], in_13[19], in_14[19], in_15[19], in_16[19], in_17[19], in_18[19], in_19[19], in_20[19], in_21[19], in_22[19], in_23[19], in_24[19], in_25[19], in_26[19], in_27[19], in_28[19], in_29[19], in_30[19], in_31[19], in_32[19]};
  assign _20 = {in_1[20], in_2[20], in_3[20], in_4[20], in_5[20], in_6[20], in_7[20], in_8[20], in_9[20], in_10[20], in_11[20], in_12[20], in_13[20], in_14[20], in_15[20], in_16[20], in_17[20], in_18[20], in_19[20], in_20[20], in_21[20], in_22[20], in_23[20], in_24[20], in_25[20], in_26[20], in_27[20], in_28[20], in_29[20], in_30[20], in_31[20], in_32[20]};
  assign _21 = {in_1[21], in_2[21], in_3[21], in_4[21], in_5[21], in_6[21], in_7[21], in_8[21], in_9[21], in_10[21], in_11[21], in_12[21], in_13[21], in_14[21], in_15[21], in_16[21], in_17[21], in_18[21], in_19[21], in_20[21], in_21[21], in_22[21], in_23[21], in_24[21], in_25[21], in_26[21], in_27[21], in_28[21], in_29[21], in_30[21], in_31[21], in_32[21]};
  assign _22 = {in_1[22], in_2[22], in_3[22], in_4[22], in_5[22], in_6[22], in_7[22], in_8[22], in_9[22], in_10[22], in_11[22], in_12[22], in_13[22], in_14[22], in_15[22], in_16[22], in_17[22], in_18[22], in_19[22], in_20[22], in_21[22], in_22[22], in_23[22], in_24[22], in_25[22], in_26[22], in_27[22], in_28[22], in_29[22], in_30[22], in_31[22], in_32[22]};
  assign _23 = {in_1[23], in_2[23], in_3[23], in_4[23], in_5[23], in_6[23], in_7[23], in_8[23], in_9[23], in_10[23], in_11[23], in_12[23], in_13[23], in_14[23], in_15[23], in_16[23], in_17[23], in_18[23], in_19[23], in_20[23], in_21[23], in_22[23], in_23[23], in_24[23], in_25[23], in_26[23], in_27[23], in_28[23], in_29[23], in_30[23], in_31[23], in_32[23]};
  assign _24 = {in_1[24], in_2[24], in_3[24], in_4[24], in_5[24], in_6[24], in_7[24], in_8[24], in_9[24], in_10[24], in_11[24], in_12[24], in_13[24], in_14[24], in_15[24], in_16[24], in_17[24], in_18[24], in_19[24], in_20[24], in_21[24], in_22[24], in_23[24], in_24[24], in_25[24], in_26[24], in_27[24], in_28[24], in_29[24], in_30[24], in_31[24], in_32[24]};
  assign _25 = {in_1[25], in_2[25], in_3[25], in_4[25], in_5[25], in_6[25], in_7[25], in_8[25], in_9[25], in_10[25], in_11[25], in_12[25], in_13[25], in_14[25], in_15[25], in_16[25], in_17[25], in_18[25], in_19[25], in_20[25], in_21[25], in_22[25], in_23[25], in_24[25], in_25[25], in_26[25], in_27[25], in_28[25], in_29[25], in_30[25], in_31[25], in_32[25]};
  assign _26 = {in_1[26], in_2[26], in_3[26], in_4[26], in_5[26], in_6[26], in_7[26], in_8[26], in_9[26], in_10[26], in_11[26], in_12[26], in_13[26], in_14[26], in_15[26], in_16[26], in_17[26], in_18[26], in_19[26], in_20[26], in_21[26], in_22[26], in_23[26], in_24[26], in_25[26], in_26[26], in_27[26], in_28[26], in_29[26], in_30[26], in_31[26], in_32[26]};
  assign _27 = {in_1[27], in_2[27], in_3[27], in_4[27], in_5[27], in_6[27], in_7[27], in_8[27], in_9[27], in_10[27], in_11[27], in_12[27], in_13[27], in_14[27], in_15[27], in_16[27], in_17[27], in_18[27], in_19[27], in_20[27], in_21[27], in_22[27], in_23[27], in_24[27], in_25[27], in_26[27], in_27[27], in_28[27], in_29[27], in_30[27], in_31[27], in_32[27]};
  assign _28 = {in_1[28], in_2[28], in_3[28], in_4[28], in_5[28], in_6[28], in_7[28], in_8[28], in_9[28], in_10[28], in_11[28], in_12[28], in_13[28], in_14[28], in_15[28], in_16[28], in_17[28], in_18[28], in_19[28], in_20[28], in_21[28], in_22[28], in_23[28], in_24[28], in_25[28], in_26[28], in_27[28], in_28[28], in_29[28], in_30[28], in_31[28], in_32[28]};
  assign _29 = {in_1[29], in_2[29], in_3[29], in_4[29], in_5[29], in_6[29], in_7[29], in_8[29], in_9[29], in_10[29], in_11[29], in_12[29], in_13[29], in_14[29], in_15[29], in_16[29], in_17[29], in_18[29], in_19[29], in_20[29], in_21[29], in_22[29], in_23[29], in_24[29], in_25[29], in_26[29], in_27[29], in_28[29], in_29[29], in_30[29], in_31[29], in_32[29]};
  assign _30 = {in_1[30], in_2[30], in_3[30], in_4[30], in_5[30], in_6[30], in_7[30], in_8[30], in_9[30], in_10[30], in_11[30], in_12[30], in_13[30], in_14[30], in_15[30], in_16[30], in_17[30], in_18[30], in_19[30], in_20[30], in_21[30], in_22[30], in_23[30], in_24[30], in_25[30], in_26[30], in_27[30], in_28[30], in_29[30], in_30[30], in_31[30], in_32[30]};
  assign _31 = {in_1[31], in_2[31], in_3[31], in_4[31], in_5[31], in_6[31], in_7[31], in_8[31], in_9[31], in_10[31], in_11[31], in_12[31], in_13[31], in_14[31], in_15[31], in_16[31], in_17[31], in_18[31], in_19[31], in_20[31], in_21[31], in_22[31], in_23[31], in_24[31], in_25[31], in_26[31], in_27[31], in_28[31], in_29[31], in_30[31], in_31[31], in_32[31]};

  // Other names for the same wires on the sheet: _15_t[31:0] = in_16; _14_t[31:0] = in_15; _13_t[31:0] = in_14;
  //   _12_t[31:0] = in_13; _11_t[31:0] = in_12; _10_t[31:0] = in_11; _9_t[31:0] = in_10; _8_t[31:0] = in_9;
  //   _7_t[31:0] = in_8; _6_t[31:0] = in_7; _5_t[31:0] = in_6; _4_t[31:0] = in_5; _3_t[31:0] = in_4;
  //   _2_t[31:0] = in_3; _1_t[31:0] = in_2; _0_t[31:0] = in_1; _16_t[31:0] = in_17; _31_t[31:0] = in_32;
  //   _30_t[31:0] = in_31; _29_t[31:0] = in_30; _28_t[31:0] = in_29; _27_t[31:0] = in_28; _26_t[31:0] = in_27;
  //   _25_t[31:0] = in_26; _24_t[31:0] = in_25; _23_t[31:0] = in_24; _22_t[31:0] = in_23; _21_t[31:0] = in_22;
  //   _20_t[31:0] = in_21; _19_t[31:0] = in_20; _18_t[31:0] = in_19; _17_t[31:0] = in_18
endmodule

module Walls (
  input  clk,
  input  [31:0] bull,
  input  init,
  input  [31:0] bull_2,
  output out_5,
  output out_6,
  output [31:0] wall
);

  wire and_2_out, and_3_out, and_4_out, cdm_8_mark5_1_data_inst, cdm_8_mark5_1_mem_cycle, clk_t, clr,
       collision_1_trigger, collision_2_trigger, comparator_1_eq, comparator_2_eq, d_ff_1_q, d_ff_2_q,
       decoder_1_out0, decoder_1_out1, decoder_3_out0, decoder_3_out1, decoder_3_out2, decoder_3_out3,
       decoder_3_out4, decoder_3_out5, decoder_3_out6, decoder_3_out7, decoder_3_out15, DONE, I_O_sel,
       multiplexer_1_out, not_1_out, not_2_out, not_3_out, not_4_out, or32_1_out, or_1_out, or_3_out,
       or_4_out, or_5_out, or_6_out, or_7_out, r, r_w, register_1_q, register_2_q, w;
  wire [2:0] counter_1_q;
  wire [7:0] addr, arr0, arr1, arr2, arr3, arr4, arr5, arr6, arr7, arr8, cdm_8_mark5_1_data_out,
       cdm_8_mark5_1_ps, cdm_8_mark5_1_r0, cdm_8_mark5_1_r1, cdm_8_mark5_1_r2, cdm_8_mark5_1_r3,
       cdm_8_mark5_1_sp, controlled_buffer_2_out, controlled_buffer_3_out, demultiplexer_1_out0,
       demultiplexer_1_out1, demultiplexer_1_out2, demultiplexer_1_out3, io_data, multiplexer_2_out, Oarr4,
       Oarr5, Oarr6, Oarr7, Oarr8, PC;
  wire [31:0] collision_1_out, collision_2_out, or_2_out;

  and and_1 (I_O_sel, and_3_out, decoder_1_out1);
  and and_2 (and_2_out, out_6, ~not_1_out, init);  // AND_Gate
  Clock \u_Частота_процессора  (.out(clk_t));
  D_Flip_Flop #(.trigger("falling")) d_ff_1 (
    .Q(d_ff_1_q), .preset(comparator_1_eq), .reset(d_ff_2_q));  // open: clk, D, Qn, en
  Comparator comparator_1 (.a(PC), .b(8'hc), .eq(comparator_1_eq));  // open: gt, lt
  D_Flip_Flop #(.trigger("falling")) d_ff_2 (.clk(clk_t), .D(and_2_out), .Q(d_ff_2_q));  // open: Qn, preset, en, reset
  D_Flip_Flop d_ff_3 (.Q(out_6), .preset(register_1_q), .reset(DONE));  // open: clk, D, Qn, en
  Register #(.width(1)) register_1 (.D(or_1_out), .Q(register_1_q), .clk(clk));  // open: en, clr
  or or_1 (or_1_out, collision_1_trigger, collision_2_trigger);
  and and_3 (and_3_out, addr[4], addr[5], addr[6], addr[7], decoder_1_out1);
  // Probe on cdm_8_mark5_1_r1
  // Probe on cdm_8_mark5_1_r3
  // Probe on cdm_8_mark5_1_r2
  // Probe on cdm_8_mark5_1_r0
  Multiplexer #(.enable("false")) multiplexer_1 (.in0(1'b0), .in1(clk_t), .out(multiplexer_1_out), .sel(not_1_out));
  Collision collision_1 (.OUT(collision_1_out), .A(bull_2), .B(wall), .Trigger(collision_1_trigger));
  and and_4 (and_4_out, decoder_1_out1, ~and_3_out);  // AND_Gate
  // Probe on PC
  // Probe on cdm_8_mark5_1_ps
  // Probe on cdm_8_mark5_1_sp
  CdM_8_mark5 cdm_8_mark5_1 (
    .clock(multiplexer_1_out), .addr(addr), .mem_read(r_w), .mem_cycle(cdm_8_mark5_1_mem_cycle),
    .data_inst(cdm_8_mark5_1_data_inst), .data_out(cdm_8_mark5_1_data_out),
    .data_in(controlled_buffer_2_out), .r0(cdm_8_mark5_1_r0), .r1(cdm_8_mark5_1_r1), .r2(cdm_8_mark5_1_r2),
    .r3(cdm_8_mark5_1_r3), .PC(PC), .SP(cdm_8_mark5_1_sp), .PS(cdm_8_mark5_1_ps));  // open: IAck, IRQ, vec, reset
  not not_1 (not_1_out, d_ff_1_q);
  Collision collision_2 (.OUT(collision_2_out), .A(bull), .B(wall), .Trigger(collision_2_trigger));
  Register #(.width(1)) register_2 (.D(collision_2_trigger), .Q(register_2_q), .clk(clk));  // open: en, clr
  Decoder #(.disabled(0)) decoder_1 (
    .out0(decoder_1_out0), .out1(decoder_1_out1), .sel(cdm_8_mark5_1_data_inst), .en(cdm_8_mark5_1_mem_cycle));
  not not_2 (not_2_out, r_w);
  assign io_data = not_2_out ? cdm_8_mark5_1_data_out : 8'bz;  // Controlled_Buffer controlled_buffer_1
  assign controlled_buffer_2_out = r_w ? io_data : 8'bz;  // Controlled_Buffer controlled_buffer_2
  D_Flip_Flop d_ff_4 (.Q(out_5), .preset(register_2_q), .reset(DONE));  // open: clk, D, Qn, en
  Or32 or32_1 (.in(or_2_out), .out(or32_1_out));
  assign or_2_out = collision_2_out | collision_1_out;  // OR_Gate or_2, 32 bits wide
  // Probe on addr
  Register #(.width(32)) register_3 (
    .D(or_2_out), .en(or32_1_out), .Q({arr7, arr6, arr5, arr4}), .clk(clk));  // open: clr
  // Probe on io_data
  RAM ram_1 (.addr(addr), .data(io_data), .sel(and_4_out), .clk(clk_t), .ld(r_w), .clr(clr));
  ROM rom_1 (.addr(addr), .data(io_data), .sel(decoder_1_out0));
  Decoder decoder_2 (.out0(r), .out1(w), .sel(r_w), .en(I_O_sel));
  Pull_Resistor pull_resistor_1 (.node(r));
  Pull_Resistor pull_resistor_2 (.node(w));
  or or_3 (or_3_out, r, w);
  assign controlled_buffer_3_out = r ? io_data : 8'bz;  // Controlled_Buffer controlled_buffer_3
  Demultiplexer #(.select(4), .width(8)) demultiplexer_1 (
    .out0(demultiplexer_1_out0), .out1(demultiplexer_1_out1), .out2(demultiplexer_1_out2),
    .out3(demultiplexer_1_out3), .out15(arr8), .in(controlled_buffer_3_out), .sel(addr[3:0]), .en(r));  // open: out4, out5, out6, out7, out8, out9, out10, out11, out12, out13, out14
  Decoder #(.select(4)) decoder_3 (
    .out0(decoder_3_out0), .out1(decoder_3_out1), .out2(decoder_3_out2), .out3(decoder_3_out3),
    .out4(decoder_3_out4), .out5(decoder_3_out5), .out6(decoder_3_out6), .out7(decoder_3_out7),
    .out15(decoder_3_out15), .sel(addr[3:0]), .en(or_3_out));  // open: out8, out9, out10, out11, out12, out13, out14
  Pull_Resistor pull_resistor_3 (.node(decoder_3_out0));
  Pull_Resistor pull_resistor_4 (.node(decoder_3_out1));
  Pull_Resistor pull_resistor_5 (.node(decoder_3_out2));
  Pull_Resistor pull_resistor_6 (.node(decoder_3_out3));
  Pull_Resistor pull_resistor_7 (.node(decoder_3_out15));
  // Probe on addr[3:0]
  Pull_Resistor pull_resistor_8 (.node(decoder_3_out4));
  Pull_Resistor pull_resistor_9 (.node(decoder_3_out5));
  Pull_Resistor pull_resistor_10 (.node(decoder_3_out6));
  Pull_Resistor pull_resistor_11 (.node(decoder_3_out7));
  assign arr0 = r ? demultiplexer_1_out0 : 8'bz;  // Controlled_Buffer controlled_buffer_4
  assign arr1 = r ? demultiplexer_1_out1 : 8'bz;  // Controlled_Buffer controlled_buffer_5
  assign arr2 = r ? demultiplexer_1_out2 : 8'bz;  // Controlled_Buffer controlled_buffer_6
  assign arr3 = r ? demultiplexer_1_out3 : 8'bz;  // Controlled_Buffer controlled_buffer_7
  not not_3 (not_3_out, out_6);
  assign io_data = w ? multiplexer_2_out : 8'bz;  // Controlled_Buffer controlled_buffer_8
  Multiplexer #(.select(4), .width(8)) multiplexer_2 (
    .in0(wall[7:0]), .in1(wall[15:8]), .in2(wall[23:16]), .in3(wall[31:24]), .in4(arr4), .in5(arr5),
    .in6(arr6), .in7(arr7), .in15(arr8), .out(multiplexer_2_out), .sel(addr[3:0]), .en(w));  // open: in8, in9, in10, in11, in12, in13, in14
  or or_4 (or_4_out, decoder_3_out4, out_6);
  or or_5 (or_5_out, decoder_3_out5, out_6);
  or or_6 (or_6_out, decoder_3_out6, out_6);
  or or_7 (or_7_out, decoder_3_out7, out_6);
  Counter #(.width(3), .max('h2)) counter_1 (
    .count(decoder_3_out3), .Q(counter_1_q), .clk(decoder_3_out3), .clr(not_3_out));  // open: load, D, carry
  Comparator #(.width(3), .mode("unsigned")) comparator_2 (
    .a(counter_1_q), .b(3'b010), .eq(comparator_2_eq));  // open: gt, lt
  Register register_4 (.D(arr0), .en(decoder_3_out0), .Q(wall[7:0]), .clk(clk_t));  // open: clr
  Register register_5 (.D(arr1), .en(decoder_3_out1), .Q(wall[15:8]), .clk(clk_t));  // open: clr
  Register register_6 (.D(arr2), .en(decoder_3_out2), .Q(wall[23:16]), .clk(clk_t));  // open: clr
  Register register_7 (.D(arr3), .en(decoder_3_out3), .Q(wall[31:24]), .clk(clk_t));  // open: clr
  Register register_8 (.D(arr4), .en(or_4_out), .Q(Oarr4), .clk(clk_t));  // open: clr
  Register register_9 (.D(arr5), .en(or_5_out), .Q(Oarr5), .clk(clk_t));  // open: clr
  Register register_10 (.D(arr6), .en(or_6_out), .Q(Oarr6), .clk(clk_t));  // open: clr
  Register register_11 (.D(arr7), .en(or_7_out), .Q(Oarr7), .clk(clk_t));  // open: clr
  Register register_12 (.D(arr8), .en(decoder_3_out15), .Q(Oarr8), .clk(clk_t));  // open: clr
  Register #(.width(1)) register_13 (
    .D(comparator_2_eq), .Q(DONE), .clk(comparator_2_eq), .clr(not_4_out));  // open: en
  not not_4 (not_4_out, out_6);

  // Other names for the same wires on the sheet: IOaddr[3:0] = addr[3:0]; BOOM = out_6; BOOMmon = out_5; gen = clk;
  //   StartGame = init; Oarr0[7:0] = wall[7:0]; Oarr1[7:0] = wall[15:8]; Oarr2[7:0] = wall[23:16];
  //   Oarr3[7:0] = wall[31:24]

  // Notes on the sheet:
  //   contents of rom_1 (hex, n*v repeats v):
  //   d0 3c d1 f0 a4 8d a4 8d a4 8d a4 c0 c4 d0 f0 d1 f4 d3 3 f eb 21 c3 b2 b7 6b a3 8c 8d c7 8b ee 13 d6
  //   c d4 209*0 4 4
  //   stack
  //   Указывает, завершилась ли обработка попадания
  //   walls
  //   hits
endmodule

module Collision (
  input  [31:0] A,
  input  [31:0] B,
  output [31:0] OUT,
  output Trigger
);

  assign OUT = A & B;  // AND_Gate and_1, 32 bits wide
  Or32 or32_1 (.in(OUT), .out(Trigger));
endmodule

module Shooting (
  input  clk,
  input  [4:0] coord,
  input  fire,
  input  reset,
  output [31:0] _2,
  output [31:0] out_6,
  output [31:0] out_7,
  output [31:0] out_8,
  output [31:0] out_9,
  output [31:0] _3,
  output [31:0] out_11,
  output [31:0] out_12,
  output [31:0] out_13,
  output [31:0] out_14,
  output [31:0] out_15,
  output [31:0] out_16,
  output [31:0] out_17,
  output [31:0] out_18,
  output [31:0] out_19,
  output [31:0] out_20,
  output [31:0] out_21,
  output [31:0] out_22,
  output [31:0] out_23,
  output [31:0] out_24,
  output [4:0] \Номер ,
  output [31:0] out_26,
  output [31:0] out_27,
  output [31:0] out_28,
  output [31:0] out_29,
  output [31:0] out_30,
  output [31:0] out_31,
  output [31:0] out_32,
  output [31:0] out_33,
  output [31:0] out_34,
  output [31:0] _31
);

  wire clock_1_out, controlled_buffer_1_out, controlled_buffer_2_out, counter_1_carry, fire_t, not_1_out,
       or_1_out, or_2_out, started;
  wire [4:0] counter_1_q, register_1_q;
  wire [31:0] demultiplexer_1_out0, demultiplexer_1_out1, demultiplexer_1_out2, demultiplexer_1_out3,
       demultiplexer_1_out4, demultiplexer_1_out5, demultiplexer_1_out6, demultiplexer_1_out7,
       demultiplexer_1_out8, demultiplexer_1_out9, demultiplexer_1_out10, demultiplexer_1_out11,
       demultiplexer_1_out12, demultiplexer_1_out13, demultiplexer_1_out14, demultiplexer_1_out15,
       demultiplexer_1_out16, demultiplexer_1_out17, demultiplexer_1_out18, demultiplexer_1_out19,
       demultiplexer_1_out20, demultiplexer_1_out21, demultiplexer_1_out22, demultiplexer_1_out23,
       demultiplexer_1_out24, demultiplexer_1_out25, demultiplexer_1_out26, demultiplexer_1_out27,
       demultiplexer_1_out28, demultiplexer_1_out29, demultiplexer_1_out30, demultiplexer_1_out31, st;

  not not_1 (not_1_out, started);
  D_Flip_Flop d_ff_1 (.Q(fire_t), .preset(controlled_buffer_1_out), .reset(clock_1_out));  // open: clk, D, Qn, en
  assign controlled_buffer_1_out = not_1_out ? fire : 1'bz;  // Controlled_Buffer controlled_buffer_1
  Pull_Resistor pull_resistor_1 (.node(controlled_buffer_1_out));
  Clock #(.highDuration(2), .lowDuration(2)) clock_1 (.out(clock_1_out));
  Transpon_field transpon_field_1 (
    .in_1(demultiplexer_1_out0), .in_2(demultiplexer_1_out1), .in_3(demultiplexer_1_out2),
    .in_4(demultiplexer_1_out3), .in_5(demultiplexer_1_out4), .in_6(demultiplexer_1_out5),
    .in_7(demultiplexer_1_out6), .in_8(demultiplexer_1_out7), .in_9(demultiplexer_1_out8),
    .in_10(demultiplexer_1_out9), .in_11(demultiplexer_1_out10), .in_12(demultiplexer_1_out11),
    .in_13(demultiplexer_1_out12), .in_14(demultiplexer_1_out13), .in_15(demultiplexer_1_out14),
    .in_16(demultiplexer_1_out15), .in_17(demultiplexer_1_out16), .in_18(demultiplexer_1_out17),
    .in_19(demultiplexer_1_out18), .in_20(demultiplexer_1_out19), .in_21(demultiplexer_1_out20),
    .in_22(demultiplexer_1_out21), .in_23(demultiplexer_1_out22), .in_24(demultiplexer_1_out23),
    .in_25(demultiplexer_1_out24), .in_26(demultiplexer_1_out25), .in_27(demultiplexer_1_out26),
    .in_28(demultiplexer_1_out27), .in_29(demultiplexer_1_out28), .in_30(demultiplexer_1_out29),
    .in_31(demultiplexer_1_out30), .in_32(demultiplexer_1_out31), ._2(_2), ._3(_3), ._4(out_15), ._5(out_20),
    ._6(out_26), ._7(out_31), ._8(out_6), ._9(out_11), ._10(out_16), ._11(out_21), ._12(out_27),
    ._13(out_32), ._14(out_7), ._15(out_12), ._16(out_17), ._17(out_22), ._18(out_28), ._19(out_33),
    ._20(out_8), ._21(out_13), ._22(out_18), ._23(out_23), ._24(out_29), ._25(out_34), ._26(out_9),
    ._27(out_14), ._29(out_24), ._30(out_30), ._31(_31), ._28(out_19));  // open: _0, _1
  Demultiplexer #(.select(5), .width(32), .enable("false")) demultiplexer_1 (
    .out0(demultiplexer_1_out0), .out1(demultiplexer_1_out1), .out2(demultiplexer_1_out2),
    .out3(demultiplexer_1_out3), .out4(demultiplexer_1_out4), .out5(demultiplexer_1_out5),
    .out6(demultiplexer_1_out6), .out7(demultiplexer_1_out7), .out8(demultiplexer_1_out8),
    .out9(demultiplexer_1_out9), .out10(demultiplexer_1_out10), .out11(demultiplexer_1_out11),
    .out12(demultiplexer_1_out12), .out13(demultiplexer_1_out13), .out14(demultiplexer_1_out14),
    .out15(demultiplexer_1_out15), .out16(demultiplexer_1_out16), .out17(demultiplexer_1_out17),
    .out18(demultiplexer_1_out18), .out19(demultiplexer_1_out19), .out20(demultiplexer_1_out20),
    .out21(demultiplexer_1_out21), .out22(demultiplexer_1_out22), .out23(demultiplexer_1_out23),
    .out24(demultiplexer_1_out24), .out25(demultiplexer_1_out25), .out26(demultiplexer_1_out26),
    .out27(demultiplexer_1_out27), .out28(demultiplexer_1_out28), .out29(demultiplexer_1_out29),
    .out30(demultiplexer_1_out30), .out31(demultiplexer_1_out31), .in(st), .sel(register_1_q));
  Register #(.width(5)) register_1 (.D(coord), .en(fire_t), .Q(register_1_q), .clk(fire_t));  // open: clr
  assign controlled_buffer_2_out = started ? clk : 1'bz;  // Controlled_Buffer controlled_buffer_2
  Counter #(.width(5), .max('h1e)) counter_1 (
    .Q(counter_1_q), .carry(counter_1_carry), .clk(controlled_buffer_2_out), .clr(or_1_out));  // open: load, D, count
  or or_1 (or_1_out, reset, ~started);  // OR_Gate
  D_Flip_Flop d_ff_2 (.Q(started), .preset(fire_t), .reset(or_2_out));  // open: clk, D, Qn, en
  or or_2 (or_2_out, reset, counter_1_carry);
  Inc_5bit inc_5bit_1 (.X(counter_1_q), .R(\Номер ));  // open: Cout
  Decoder #(.select(5), .enable("false")) decoder_1 (
    .out0(st[0]), .out1(st[1]), .out2(st[2]), .out3(st[3]), .out4(st[4]), .out5(st[5]), .out6(st[6]),
    .out7(st[7]), .out8(st[8]), .out9(st[9]), .out10(st[10]), .out11(st[11]), .out12(st[12]), .out13(st[13]),
    .out14(st[14]), .out15(st[15]), .out16(st[16]), .out17(st[17]), .out18(st[18]), .out19(st[19]),
    .out20(st[20]), .out21(st[21]), .out22(st[22]), .out23(st[23]), .out24(st[24]), .out25(st[25]),
    .out26(st[26]), .out27(st[27]), .out28(st[28]), .out29(st[29]), .out30(st[30]), .out31(st[31]),
    .sel(\Номер ));

  // Other names for the same wires on the sheet: _4[31:0] = out_15; _5[31:0] = out_20; _6[31:0] = out_26;
  //   _7[31:0] = out_31; _8[31:0] = out_6; _9[31:0] = out_11; _10[31:0] = out_16; _11[31:0] = out_21;
  //   _12[31:0] = out_27; _13[31:0] = out_32; _14[31:0] = out_7; _15[31:0] = out_12; _16[31:0] = out_17;
  //   _17[31:0] = out_22; _18[31:0] = out_28; _19[31:0] = out_33; _20[31:0] = out_8; _21[31:0] = out_13;
  //   _22[31:0] = out_18; _23[31:0] = out_23; _24[31:0] = out_29; _25[31:0] = out_34; _26[31:0] = out_9;
  //   _27[31:0] = out_14; _28[31:0] = out_19; _29[31:0] = out_24; _30[31:0] = out_30

  // Notes on the sheet:
  //   Столбец из пуль
endmodule

module Menu (
  input  [4:0] in,
  output [31:0] out
);

  wire decoder_1_out0, decoder_1_out1, decoder_1_out2, decoder_1_out3, decoder_1_out4, decoder_1_out5,
       decoder_1_out6, decoder_1_out7, decoder_1_out8, decoder_1_out9, decoder_1_out10, decoder_1_out11,
       decoder_1_out12, decoder_1_out13, decoder_1_out14, decoder_1_out15, decoder_1_out16, decoder_1_out17,
       decoder_1_out18, decoder_1_out19, decoder_1_out20, decoder_1_out21, decoder_1_out22, decoder_1_out23,
       decoder_1_out24, decoder_1_out25, decoder_1_out26, decoder_1_out27, decoder_1_out28, decoder_1_out29,
       decoder_1_out30, decoder_1_out31;
  wire [31:0] pull_resistor_1_node, pull_resistor_2_node, pull_resistor_3_node;

  Pull_Resistor pull_resistor_1 (.node(pull_resistor_1_node));
  Pull_Resistor pull_resistor_2 (.node(pull_resistor_2_node));
  Pull_Resistor pull_resistor_3 (.node(pull_resistor_3_node));
  Decoder #(.select(5), .disabled(0), .enable("false")) decoder_1 (
    .out0(decoder_1_out0), .out1(decoder_1_out1), .out2(decoder_1_out2), .out3(decoder_1_out3),
    .out4(decoder_1_out4), .out5(decoder_1_out5), .out6(decoder_1_out6), .out7(decoder_1_out7),
    .out8(decoder_1_out8), .out9(decoder_1_out9), .out10(decoder_1_out10), .out11(decoder_1_out11),
    .out12(decoder_1_out12), .out13(decoder_1_out13), .out14(decoder_1_out14), .out15(decoder_1_out15),
    .out16(decoder_1_out16), .out17(decoder_1_out17), .out18(decoder_1_out18), .out19(decoder_1_out19),
    .out20(decoder_1_out20), .out21(decoder_1_out21), .out22(decoder_1_out22), .out23(decoder_1_out23),
    .out24(decoder_1_out24), .out25(decoder_1_out25), .out26(decoder_1_out26), .out27(decoder_1_out27),
    .out28(decoder_1_out28), .out29(decoder_1_out29), .out30(decoder_1_out30), .out31(decoder_1_out31),
    .sel(in));
  assign out = decoder_1_out28 ? pull_resistor_3_node : 32'bz;  // Controlled_Buffer controlled_buffer_1
  assign out = decoder_1_out29 ? pull_resistor_3_node : 32'bz;  // Controlled_Buffer controlled_buffer_2
  assign out = decoder_1_out30 ? pull_resistor_3_node : 32'bz;  // Controlled_Buffer controlled_buffer_3
  assign out = decoder_1_out31 ? pull_resistor_3_node : 32'bz;  // Controlled_Buffer controlled_buffer_4
  assign out = decoder_1_out25 ? 32'h45141040 : 32'bz;  // Controlled_Buffer controlled_buffer_5
  assign out = decoder_1_out26 ? 32'h45141040 : 32'bz;  // Controlled_Buffer controlled_buffer_6
  assign out = decoder_1_out27 ? 32'h7df7df7c : 32'bz;  // Controlled_Buffer controlled_buffer_7
  assign out = decoder_1_out22 ? 32'h41840104 : 32'bz;  // Controlled_Buffer controlled_buffer_8
  assign out = decoder_1_out23 ? 32'h7df7df7c : 32'bz;  // Controlled_Buffer controlled_buffer_9
  assign out = decoder_1_out24 ? 32'h45141040 : 32'bz;  // Controlled_Buffer controlled_buffer_10
  assign out = decoder_1_out1 ? pull_resistor_1_node : 32'bz;  // Controlled_Buffer controlled_buffer_11
  assign out = decoder_1_out2 ? pull_resistor_1_node : 32'bz;  // Controlled_Buffer controlled_buffer_12
  assign out = decoder_1_out3 ? pull_resistor_1_node : 32'bz;  // Controlled_Buffer controlled_buffer_13
  assign out = decoder_1_out4 ? pull_resistor_1_node : 32'bz;  // Controlled_Buffer controlled_buffer_14
  assign out = decoder_1_out5 ? 32'h7c445108 : 32'bz;  // Controlled_Buffer controlled_buffer_15
  assign out = decoder_1_out6 ? 32'h4445208 : 32'bz;  // Controlled_Buffer controlled_buffer_16
  assign out = decoder_1_out7 ? 32'h4445808 : 32'bz;  // Controlled_Buffer controlled_buffer_17
  assign out = decoder_1_out8 ? 32'h7c47df88 : 32'bz;  // Controlled_Buffer controlled_buffer_18
  assign out = decoder_1_out9 ? 32'h40445088 : 32'bz;  // Controlled_Buffer controlled_buffer_19
  assign out = decoder_1_out10 ? 32'h40445088 : 32'bz;  // Controlled_Buffer controlled_buffer_20
  assign out = decoder_1_out11 ? 32'h40445088 : 32'bz;  // Controlled_Buffer controlled_buffer_21
  assign out = decoder_1_out12 ? 32'h7df7dfbe : 32'bz;  // Controlled_Buffer controlled_buffer_22
  assign out = decoder_1_out13 ? pull_resistor_2_node : 32'bz;  // Controlled_Buffer controlled_buffer_23
  assign out = decoder_1_out14 ? pull_resistor_2_node : 32'bz;  // Controlled_Buffer controlled_buffer_24
  assign out = decoder_1_out15 ? pull_resistor_2_node : 32'bz;  // Controlled_Buffer controlled_buffer_25
  assign out = decoder_1_out16 ? pull_resistor_2_node : 32'bz;  // Controlled_Buffer controlled_buffer_26
  assign out = decoder_1_out17 ? pull_resistor_2_node : 32'bz;  // Controlled_Buffer controlled_buffer_27
  assign out = decoder_1_out18 ? pull_resistor_2_node : 32'bz;  // Controlled_Buffer controlled_buffer_28
  assign out = decoder_1_out19 ? pull_resistor_2_node : 32'bz;  // Controlled_Buffer controlled_buffer_29
  assign out = decoder_1_out20 ? 32'h4117df7c : 32'bz;  // Controlled_Buffer controlled_buffer_30
  assign out = decoder_1_out21 ? 32'h41240104 : 32'bz;  // Controlled_Buffer controlled_buffer_31
  assign out = decoder_1_out0 ? pull_resistor_1_node : 32'bz;  // Controlled_Buffer controlled_buffer_32
endmodule

module Circ (
  input  on,
  input  isgameover,
  input  start,
  input  [4:0] counter,
  input  [31:0] game,
  input  endgame,
  output [31:0] out_7
);

  wire and_1_out, and_2_out, not_1_out;
  wire [31:0] gameover_1_out, menu_1_out;

  not not_1 (not_1_out, on);
  and and_1 (and_1_out, on, ~start);  // AND_Gate
  Menu menu_1 (.in(counter), .out(menu_1_out));
  and and_2 (and_2_out, on, ~endgame, start);  // AND_Gate
  assign out_7 = not_1_out ? {32{1'b0}} : 32'bz;  // Controlled_Buffer controlled_buffer_1
  assign out_7 = and_1_out ? menu_1_out : 32'bz;  // Controlled_Buffer controlled_buffer_2
  assign out_7 = and_2_out ? game : 32'bz;  // Controlled_Buffer controlled_buffer_3
  Gameover gameover_1 (.in(counter), .isGameOver(isgameover), .out(gameover_1_out));
  assign out_7 = endgame ? gameover_1_out : 32'bz;  // Controlled_Buffer controlled_buffer_4
endmodule

module Menumega (
  input  gameover,
  input  endgame,
  input  on,
  input  [4:0] beg,
  input  start,
  input  [31:0] in_6,
  input  [31:0] in_7,
  input  [31:0] in_8,
  input  [31:0] in_9,
  input  [31:0] in_10,
  input  [31:0] in_11,
  input  [31:0] in_12,
  input  [31:0] in_13,
  output [31:0] out_14,
  output [31:0] out_15,
  output [31:0] out_16,
  output [31:0] out_17,
  output [31:0] out_18,
  output [31:0] out_19,
  output [31:0] out_20,
  output [31:0] out_21,
  output [4:0] \end 
);

  wire [4:0] inc_5bit_1_r, inc_5bit_2_r, inc_5bit_3_r, inc_5bit_4_r, inc_5bit_5_r, inc_5bit_6_r;

  Circ circ_1 (
    .on(on), .start(start), .counter(beg), .game(in_6), .out_7(out_14), .isgameover(gameover),
    .endgame(endgame));
  Circ circ_2 (
    .on(on), .start(start), .counter(inc_5bit_1_r), .game(in_10), .out_7(out_18), .isgameover(gameover),
    .endgame(endgame));
  Circ circ_3 (
    .on(on), .start(start), .counter(inc_5bit_2_r), .game(in_7), .out_7(out_15), .isgameover(gameover),
    .endgame(endgame));
  Inc_5bit inc_5bit_1 (.X(beg), .R(inc_5bit_1_r));  // open: Cout
  Inc_5bit inc_5bit_2 (.X(inc_5bit_1_r), .R(inc_5bit_2_r));  // open: Cout
  Circ circ_4 (
    .on(on), .start(start), .counter(inc_5bit_3_r), .game(in_11), .out_7(out_19), .isgameover(gameover),
    .endgame(endgame));
  Inc_5bit inc_5bit_3 (.X(inc_5bit_2_r), .R(inc_5bit_3_r));  // open: Cout
  Inc_5bit inc_5bit_4 (.X(inc_5bit_3_r), .R(inc_5bit_4_r));  // open: Cout
  Circ circ_5 (
    .on(on), .start(start), .counter(inc_5bit_5_r), .game(in_12), .out_7(out_20), .isgameover(gameover),
    .endgame(endgame));
  Circ circ_6 (
    .on(on), .start(start), .counter(inc_5bit_4_r), .game(in_8), .out_7(out_16), .isgameover(gameover),
    .endgame(endgame));
  Inc_5bit inc_5bit_5 (.X(inc_5bit_4_r), .R(inc_5bit_5_r));  // open: Cout
  Circ circ_7 (
    .on(on), .start(start), .counter(inc_5bit_6_r), .game(in_9), .out_7(out_17), .isgameover(gameover),
    .endgame(endgame));
  Inc_5bit inc_5bit_6 (.X(inc_5bit_5_r), .R(inc_5bit_6_r));  // open: Cout
  Inc_5bit inc_5bit_7 (.X(inc_5bit_6_r), .R(\end ));  // open: Cout
  Circ circ_8 (
    .on(on), .start(start), .counter(\end ), .game(in_13), .out_7(out_21), .isgameover(gameover),
    .endgame(endgame));
endmodule

module Pentamenu (
  input  start,
  input  on,
  input  [6:0] control,
  output [31:0] out_4,
  output [31:0] out_5,
  output [31:0] out_6,
  output [31:0] out_7,
  output [31:0] out_8,
  output [31:0] out_9,
  output [31:0] out_10,
  output [31:0] out_11,
  output [31:0] out_12,
  output [31:0] out_13,
  output [31:0] out_14,
  output [31:0] out_15,
  output [31:0] out_16,
  output [31:0] out_17,
  output [31:0] out_18,
  output [31:0] out_19,
  output [31:0] out_20,
  output [31:0] out_21,
  output [31:0] out_22,
  output [31:0] out_23,
  output [31:0] out_24,
  output [31:0] out_25,
  output [31:0] out_26,
  output [31:0] out_27,
  output [31:0] out_28,
  output [31:0] out_29,
  output [31:0] out_30,
  output [31:0] out_31,
  output [31:0] out_32,
  output [31:0] out_33,
  output [31:0] out_34,
  output [31:0] out_35
);

  wire clock_1_out, d_ff_1_q, d_ff_2_q, eg, go, main_1_gameover, main_1_win, multiplexer_1_out, not_1_out,
       on_t, start_t;
  wire [4:0] menumega_1_end, menumega_2_end, menumega_3_end;
  wire [31:0] main_1_out_4, main_1_out_5, main_1_out_6, main_1_out_7, main_1_out_8, main_1_out_9,
       main_1_out_10, main_1_out_11, main_1_out_12, main_1_out_13, main_1_out_14, main_1_out_15,
       main_1_out_16, main_1_out_17, main_1_out_18, main_1_out_19, main_1_out_20, main_1_out_21,
       main_1_out_22, main_1_out_23, main_1_out_24, main_1_out_25, main_1_out_26, main_1_out_27,
       main_1_out_28, main_1_out_29, main_1_out_30, main_1_out_31, main_1_out_32, main_1_out_33,
       main_1_out_34, main_1_out_35;

  Counter #(.width(1), .max('h1)) counter_1 (.count(start), .Q(start_t), .clk(start));  // open: load, D, carry, clr
  Counter #(.width(1), .max('h1)) counter_2 (.count(on), .Q(on_t), .clk(on));  // open: load, D, carry, clr
  Main main_1 (
    .out_4(main_1_out_4), .out_8(main_1_out_8), .out_12(main_1_out_12), .out_16(main_1_out_16),
    .out_20(main_1_out_20), .out_24(main_1_out_24), .out_28(main_1_out_28), .out_32(main_1_out_32),
    .out_5(main_1_out_5), .out_9(main_1_out_9), .clk(clock_1_out), .out_13(main_1_out_13),
    .out_17(main_1_out_17), .out_21(main_1_out_21), .out_25(main_1_out_25), .initgame(start_t),
    .out_29(main_1_out_29), .out_33(main_1_out_33), .moving(control), .out_6(main_1_out_6),
    .out_10(main_1_out_10), .out_14(main_1_out_14), .out_18(main_1_out_18), .out_22(main_1_out_22),
    .out_26(main_1_out_26), .gameover(main_1_gameover), .out_30(main_1_out_30), .win(main_1_win),
    .out_34(main_1_out_34), .out_7(main_1_out_7), .out_11(main_1_out_11), .out_15(main_1_out_15),
    .out_19(main_1_out_19), .out_23(main_1_out_23), .out_27(main_1_out_27), .out_31(main_1_out_31),
    .out_35(main_1_out_35));
  D_Flip_Flop d_ff_1 (.clk(main_1_win), .D(main_1_win), .Q(d_ff_1_q));  // open: Qn, preset, en, reset
  Menumega menumega_1 (
    .beg({5{1'b0}}), .on(on_t), .start(start_t), .out_14(out_4), .out_18(out_8), .out_15(out_12),
    .out_19(out_16), .out_16(out_20), .out_20(out_24), .out_17(out_28), .out_21(out_32),
    .\end (menumega_1_end), .in_6(main_1_out_4), .in_7(main_1_out_12), .in_8(main_1_out_20),
    .in_9(main_1_out_28), .in_10(main_1_out_8), .in_11(main_1_out_16), .in_12(main_1_out_24),
    .in_13(main_1_out_32), .endgame(eg), .gameover(go));
  assign eg = not_1_out ? d_ff_1_q : 1'bz;  // Controlled_Buffer controlled_buffer_1
  Pull_Resistor pull_resistor_1 (.node(eg));
  Menumega menumega_2 (
    .beg(menumega_1_end), .on(on_t), .start(start_t), .out_14(out_5), .out_18(out_9), .out_15(out_13),
    .out_19(out_17), .out_16(out_21), .out_20(out_25), .out_17(out_29), .out_21(out_33),
    .\end (menumega_2_end), .in_6(main_1_out_5), .in_7(main_1_out_13), .in_8(main_1_out_21),
    .in_9(main_1_out_29), .in_10(main_1_out_9), .in_11(main_1_out_17), .in_12(main_1_out_25),
    .in_13(main_1_out_33), .endgame(eg), .gameover(go));
  Menumega menumega_3 (
    .beg(menumega_2_end), .on(on_t), .start(start_t), .out_14(out_6), .out_18(out_10), .out_15(out_14),
    .out_19(out_18), .out_16(out_22), .out_20(out_26), .out_17(out_30), .out_21(out_34),
    .\end (menumega_3_end), .in_6(main_1_out_6), .in_7(main_1_out_14), .in_8(main_1_out_22),
    .in_9(main_1_out_30), .in_10(main_1_out_10), .in_11(main_1_out_18), .in_12(main_1_out_26),
    .in_13(main_1_out_34), .endgame(eg), .gameover(go));
  Menumega menumega_4 (
    .beg(menumega_3_end), .on(on_t), .start(start_t), .out_14(out_7), .out_18(out_11), .out_15(out_15),
    .out_19(out_19), .out_16(out_23), .out_20(out_27), .out_17(out_31), .out_21(out_35), .in_6(main_1_out_7),
    .in_7(main_1_out_15), .in_8(main_1_out_23), .in_9(main_1_out_31), .in_10(main_1_out_11),
    .in_11(main_1_out_19), .in_12(main_1_out_27), .in_13(main_1_out_35), .endgame(eg), .gameover(go));  // open: end
  Clock clock_1 (.out(clock_1_out));
  assign eg = d_ff_2_q ? d_ff_2_q : 1'bz;  // Controlled_Buffer controlled_buffer_2
  Pull_Resistor pull_resistor_2 (.node(eg));
  D_Flip_Flop d_ff_2 (.clk(main_1_gameover), .D(main_1_gameover), .Q(d_ff_2_q));  // open: Qn, preset, en, reset
  assign go = multiplexer_1_out ? d_ff_2_q : 1'bz;  // Controlled_Buffer controlled_buffer_3
  Multiplexer multiplexer_1 (.in0(d_ff_2_q), .in1(1'b0), .out(multiplexer_1_out), .sel(d_ff_1_q));  // open: en
  not not_1 (not_1_out, d_ff_2_q);
  Pull_Resistor pull_resistor_3 (.node(go));

  // Other names for the same wires on the sheet: _0[31:0] = out_4; _1[31:0] = out_8; _2[31:0] = out_12;
  //   _3[31:0] = out_16; _4[31:0] = out_20; _5[31:0] = out_24; _6[31:0] = out_28; _7[31:0] = out_32; _8[31:0] = out_5;
  //   _9[31:0] = out_9; _10[31:0] = out_13; _11[31:0] = out_17; _12[31:0] = out_21; _13[31:0] = out_25;
  //   _14[31:0] = out_29; _15[31:0] = out_33; _16[31:0] = out_6; _17[31:0] = out_10; _18[31:0] = out_14;
  //   _19[31:0] = out_18; _20[31:0] = out_22; _21[31:0] = out_26; _22[31:0] = out_30; _23[31:0] = out_34;
  //   _24[31:0] = out_7; _25[31:0] = out_11; _26[31:0] = out_15; _27[31:0] = out_19; _28[31:0] = out_23;
  //   _29[31:0] = out_27; _30[31:0] = out_31; _31[31:0] = out_35
endmodule

module Main_Interface (
);

  wire keyboard_1_avail, ON_OFF_out, START_out, undriven;
  wire [6:0] keyboard_1_data;
  wire [31:0] pentamenu_1_out_4, pentamenu_1_out_5, pentamenu_1_out_6, pentamenu_1_out_7, pentamenu_1_out_8,
       pentamenu_1_out_9, pentamenu_1_out_10, pentamenu_1_out_11, pentamenu_1_out_12, pentamenu_1_out_13,
       pentamenu_1_out_14, pentamenu_1_out_15, pentamenu_1_out_16, pentamenu_1_out_17, pentamenu_1_out_18,
       pentamenu_1_out_19, pentamenu_1_out_20, pentamenu_1_out_21, pentamenu_1_out_22, pentamenu_1_out_23,
       pentamenu_1_out_24, pentamenu_1_out_25, pentamenu_1_out_26, pentamenu_1_out_27, pentamenu_1_out_28,
       pentamenu_1_out_29, pentamenu_1_out_30, pentamenu_1_out_31, pentamenu_1_out_32, pentamenu_1_out_33,
       pentamenu_1_out_34, pentamenu_1_out_35;

  DotMatrix #(.inputtype("row"), .matrixcols(32), .matrixrows(32)) dotmatrix_1 (
    .row0(pentamenu_1_out_35), .row1(pentamenu_1_out_31), .row2(pentamenu_1_out_27),
    .row3(pentamenu_1_out_23), .row4(pentamenu_1_out_19), .row5(pentamenu_1_out_15),
    .row6(pentamenu_1_out_11), .row7(pentamenu_1_out_7), .row8(pentamenu_1_out_34),
    .row9(pentamenu_1_out_30), .row10(pentamenu_1_out_26), .row11(pentamenu_1_out_22),
    .row12(pentamenu_1_out_18), .row13(pentamenu_1_out_14), .row14(pentamenu_1_out_10),
    .row15(pentamenu_1_out_6), .row16(pentamenu_1_out_33), .row17(pentamenu_1_out_29),
    .row18(pentamenu_1_out_25), .row19(pentamenu_1_out_21), .row20(pentamenu_1_out_17),
    .row21(pentamenu_1_out_13), .row22(pentamenu_1_out_9), .row23(pentamenu_1_out_5),
    .row24(pentamenu_1_out_32), .row25(pentamenu_1_out_28), .row26(pentamenu_1_out_24),
    .row27(pentamenu_1_out_20), .row28(pentamenu_1_out_16), .row29(pentamenu_1_out_12),
    .row30(pentamenu_1_out_8), .row31(pentamenu_1_out_4));
  Pentamenu pentamenu_1 (
    .out_4(pentamenu_1_out_4), .out_8(pentamenu_1_out_8), .start(START_out), .out_12(pentamenu_1_out_12),
    .on(ON_OFF_out), .out_16(pentamenu_1_out_16), .out_20(pentamenu_1_out_20), .out_24(pentamenu_1_out_24),
    .out_28(pentamenu_1_out_28), .control(keyboard_1_data), .out_32(pentamenu_1_out_32),
    .out_5(pentamenu_1_out_5), .out_9(pentamenu_1_out_9), .out_13(pentamenu_1_out_13),
    .out_17(pentamenu_1_out_17), .out_21(pentamenu_1_out_21), .out_25(pentamenu_1_out_25),
    .out_29(pentamenu_1_out_29), .out_33(pentamenu_1_out_33), .out_6(pentamenu_1_out_6),
    .out_10(pentamenu_1_out_10), .out_14(pentamenu_1_out_14), .out_18(pentamenu_1_out_18),
    .out_22(pentamenu_1_out_22), .out_26(pentamenu_1_out_26), .out_30(pentamenu_1_out_30),
    .out_34(pentamenu_1_out_34), .out_7(pentamenu_1_out_7), .out_11(pentamenu_1_out_11),
    .out_15(pentamenu_1_out_15), .out_19(pentamenu_1_out_19), .out_23(pentamenu_1_out_23),
    .out_27(pentamenu_1_out_27), .out_31(pentamenu_1_out_31), .out_35(pentamenu_1_out_35));
  Keyboard keyboard_1 (
    .clk(undriven), .clr(keyboard_1_avail), .avail(keyboard_1_avail), .data(keyboard_1_data));  // open: re
  Cosmsirc_nonuse cosmsirc_nonuse_1 ();
  Button ON_OFF (.out(ON_OFF_out));
  Button START (.out(START_out));
endmodule

module Gameover (
  input  [4:0] in,
  input  isGameOver,
  output [31:0] out
);

  wire decoder_1_out0, decoder_1_out1, decoder_1_out2, decoder_1_out3, decoder_1_out4, decoder_1_out5,
       decoder_1_out6, decoder_1_out7, decoder_1_out8, decoder_1_out9, decoder_1_out10, decoder_1_out11,
       decoder_1_out12, decoder_1_out13, decoder_1_out14, decoder_1_out15, decoder_1_out16, decoder_1_out17,
       decoder_1_out18, decoder_1_out19, decoder_1_out20, decoder_1_out21, decoder_1_out22, decoder_1_out23,
       decoder_1_out24, decoder_1_out25, decoder_1_out26, decoder_1_out27, decoder_1_out28, decoder_1_out29,
       decoder_1_out30, decoder_1_out31;
  wire [31:0] multiplexer_1_out, multiplexer_2_out, multiplexer_3_out, multiplexer_4_out, multiplexer_5_out,
       multiplexer_6_out, multiplexer_7_out, multiplexer_8_out, multiplexer_9_out, multiplexer_10_out,
       multiplexer_11_out, multiplexer_12_out, multiplexer_13_out, multiplexer_14_out, multiplexer_15_out,
       pull_resistor_1_node, pull_resistor_2_node, pull_resistor_3_node;

  Pull_Resistor pull_resistor_1 (.node(pull_resistor_1_node));
  Decoder #(.select(5), .disabled(0), .enable("false")) decoder_1 (
    .out0(decoder_1_out0), .out1(decoder_1_out1), .out2(decoder_1_out2), .out3(decoder_1_out3),
    .out4(decoder_1_out4), .out5(decoder_1_out5), .out6(decoder_1_out6), .out7(decoder_1_out7),
    .out8(decoder_1_out8), .out9(decoder_1_out9), .out10(decoder_1_out10), .out11(decoder_1_out11),
    .out12(decoder_1_out12), .out13(decoder_1_out13), .out14(decoder_1_out14), .out15(decoder_1_out15),
    .out16(decoder_1_out16), .out17(decoder_1_out17), .out18(decoder_1_out18), .out19(decoder_1_out19),
    .out20(decoder_1_out20), .out21(decoder_1_out21), .out22(decoder_1_out22), .out23(decoder_1_out23),
    .out24(decoder_1_out24), .out25(decoder_1_out25), .out26(decoder_1_out26), .out27(decoder_1_out27),
    .out28(decoder_1_out28), .out29(decoder_1_out29), .out30(decoder_1_out30), .out31(decoder_1_out31),
    .sel(in));
  Pull_Resistor pull_resistor_2 (.node(pull_resistor_2_node));
  Multiplexer #(.width(32)) multiplexer_1 (
    .in0(32'h1c3e840), .in1(32'h7e187e44), .out(multiplexer_1_out), .sel(isGameOver));  // open: en
  Multiplexer #(.width(32)) multiplexer_2 (
    .in0(32'h2a088c0), .in1(32'h42184048), .out(multiplexer_2_out), .sel(isGameOver));  // open: en
  Multiplexer #(.width(32)) multiplexer_3 (
    .in0(32'h2a089c0), .in1(32'h42247c60), .out(multiplexer_3_out), .sel(isGameOver));  // open: en
  Multiplexer #(.width(32)) multiplexer_4 (
    .in0(32'h6b08940), .in1(32'h2466407c), .out(multiplexer_4_out), .sel(isGameOver));  // open: en
  Multiplexer #(.width(32)) multiplexer_5 (
    .in0(32'h6b08b40), .in1(32'h42424042), .out(multiplexer_5_out), .sel(isGameOver));  // open: en
  Multiplexer #(.width(32)) multiplexer_6 (
    .in0(32'hc988e40), .in1(32'h42c34042), .out(multiplexer_6_out), .sel(isGameOver));  // open: en
  Multiplexer #(.width(32)) multiplexer_7 (
    .in0(32'hc988c40), .in1(32'h7e817e7c), .out(multiplexer_7_out), .sel(isGameOver));  // open: en
  Multiplexer #(.width(32)) multiplexer_8 (
    .in0(32'h80be840), .in1(pull_resistor_3_node), .out(multiplexer_8_out), .sel(isGameOver));  // open: en
  Pull_Resistor pull_resistor_3 (.node(pull_resistor_3_node));
  Multiplexer #(.width(32)) multiplexer_9 (
    .in0(32'h1f7df00), .in1(32'h7e42817e), .out(multiplexer_9_out), .sel(isGameOver));  // open: en
  Multiplexer #(.width(32)) multiplexer_10 (
    .in0(32'h145100), .in1(32'h42428140), .out(multiplexer_10_out), .sel(isGameOver));  // open: en
  Multiplexer #(.width(32)) multiplexer_11 (
    .in0(32'h145100), .in1(32'h407e817c), .out(multiplexer_11_out), .sel(isGameOver));  // open: en
  Multiplexer #(.width(32)) multiplexer_12 (
    .in0(32'h1f45100), .in1(32'h40429940), .out(multiplexer_12_out), .sel(isGameOver));  // open: en
  Multiplexer #(.width(32)) multiplexer_13 (
    .in0(32'h1145100), .in1(32'h4242bd40), .out(multiplexer_13_out), .sel(isGameOver));  // open: en
  Multiplexer #(.width(32)) multiplexer_14 (
    .in0(32'h1145100), .in1(32'h4242e740), .out(multiplexer_14_out), .sel(isGameOver));  // open: en
  Multiplexer #(.width(32)) multiplexer_15 (
    .in0(32'h117d100), .in1(32'h7e7ec37e), .out(multiplexer_15_out), .sel(isGameOver));  // open: en
  assign out = decoder_1_out31 ? pull_resistor_1_node : 32'bz;  // Controlled_Buffer controlled_buffer_1
  assign out = decoder_1_out27 ? multiplexer_15_out : 32'bz;  // Controlled_Buffer controlled_buffer_2
  assign out = decoder_1_out28 ? pull_resistor_1_node : 32'bz;  // Controlled_Buffer controlled_buffer_3
  assign out = decoder_1_out29 ? pull_resistor_1_node : 32'bz;  // Controlled_Buffer controlled_buffer_4
  assign out = decoder_1_out30 ? pull_resistor_1_node : 32'bz;  // Controlled_Buffer controlled_buffer_5
  assign out = decoder_1_out25 ? multiplexer_13_out : 32'bz;  // Controlled_Buffer controlled_buffer_6
  assign out = decoder_1_out26 ? multiplexer_14_out : 32'bz;  // Controlled_Buffer controlled_buffer_7
  assign out = decoder_1_out22 ? multiplexer_10_out : 32'bz;  // Controlled_Buffer controlled_buffer_8
  assign out = decoder_1_out23 ? multiplexer_11_out : 32'bz;  // Controlled_Buffer controlled_buffer_9
  assign out = decoder_1_out24 ? multiplexer_12_out : 32'bz;  // Controlled_Buffer controlled_buffer_10
  assign out = decoder_1_out1 ? pull_resistor_2_node : 32'bz;  // Controlled_Buffer controlled_buffer_11
  assign out = decoder_1_out2 ? pull_resistor_2_node : 32'bz;  // Controlled_Buffer controlled_buffer_12
  assign out = decoder_1_out3 ? pull_resistor_2_node : 32'bz;  // Controlled_Buffer controlled_buffer_13
  assign out = decoder_1_out4 ? pull_resistor_2_node : 32'bz;  // Controlled_Buffer controlled_buffer_14
  assign out = decoder_1_out5 ? multiplexer_1_out : 32'bz;  // Controlled_Buffer controlled_buffer_15
  assign out = decoder_1_out6 ? multiplexer_2_out : 32'bz;  // Controlled_Buffer controlled_buffer_16
  assign out = decoder_1_out7 ? multiplexer_3_out : 32'bz;  // Controlled_Buffer controlled_buffer_17
  assign out = decoder_1_out8 ? multiplexer_4_out : 32'bz;  // Controlled_Buffer controlled_buffer_18
  assign out = decoder_1_out9 ? multiplexer_5_out : 32'bz;  // Controlled_Buffer controlled_buffer_19
  assign out = decoder_1_out10 ? multiplexer_6_out : 32'bz;  // Controlled_Buffer controlled_buffer_20
  assign out = decoder_1_out11 ? multiplexer_7_out : 32'bz;  // Controlled_Buffer controlled_buffer_21
  assign out = decoder_1_out12 ? multiplexer_8_out : 32'bz;  // Controlled_Buffer controlled_buffer_22
  assign out = decoder_1_out13 ? pull_resistor_3_node : 32'bz;  // Controlled_Buffer controlled_buffer_23
  assign out = decoder_1_out14 ? pull_resistor_3_node : 32'bz;  // Controlled_Buffer controlled_buffer_24
  assign out = decoder_1_out15 ? pull_resistor_3_node : 32'bz;  // Controlled_Buffer controlled_buffer_25
  assign out = decoder_1_out16 ? pull_resistor_3_node : 32'bz;  // Controlled_Buffer controlled_buffer_26
  assign out = decoder_1_out17 ? pull_resistor_3_node : 32'bz;  // Controlled_Buffer controlled_buffer_27
  assign out = decoder_1_out18 ? pull_resistor_3_node : 32'bz;  // Controlled_Buffer controlled_buffer_28
  assign out = decoder_1_out19 ? pull_resistor_3_node : 32'bz;  // Controlled_Buffer controlled_buffer_29
  assign out = decoder_1_out20 ? pull_resistor_3_node : 32'bz;  // Controlled_Buffer controlled_buffer_30
  assign out = decoder_1_out21 ? multiplexer_9_out : 32'bz;  // Controlled_Buffer controlled_buffer_31
  assign out = decoder_1_out0 ? pull_resistor_2_node : 32'bz;  // Controlled_Buffer controlled_buffer_32
endmodule

module Or32 (
  input  [31:0] in,
  output out
);

  or or_1 (out, in[0], in[1], in[2], in[3], in[4], in[5], in[6], in[7], in[8], in[9], in[10], in[11], in[12], in[13], in[14], in[15], in[16], in[17], in[18], in[19], in[20], in[21], in[22], in[23], in[24], in[25], in[26], in[27], in[28], in[29], in[30], in[31]);
endmodule

module Enemies (
  input  wall,
  input  initgame,
  input  [31:0] in_3,
  input  [31:0] in_4,
  input  clk,
  input  [31:0] in_6,
  input  [31:0] in_7,
  input  [31:0] in_8,
  input  [31:0] in_9,
  input  [31:0] in_10,
  input  [31:0] in_11,
  input  [31:0] in_12,
  input  [31:0] in_13,
  input  [31:0] in_14,
  input  [31:0] in_15,
  input  [4:0] Num,
  input  [31:0] in_17,
  input  [31:0] in_18,
  input  [31:0] in_19,
  input  [31:0] in_20,
  input  [31:0] in_21,
  input  [31:0] in_22,
  input  [31:0] in_23,
  input  [31:0] in_24,
  input  [31:0] in_25,
  input  [31:0] in_26,
  input  [31:0] in_27,
  input  [31:0] in_28,
  input  [31:0] in_29,
  input  [31:0] in_30,
  input  [31:0] in_31,
  input  [31:0] in_32,
  input  [31:0] in_33,
  input  [31:0] in_34,
  output boom,
  output [31:0] out_36,
  output [31:0] out_37,
  output [31:0] out_38,
  output [31:0] out_39,
  output win,
  output [31:0] out_41,
  output [31:0] out_42,
  output [31:0] out_43,
  output [31:0] out_44,
  output [31:0] out_45,
  output [31:0] out_46,
  output [31:0] out_47,
  output [31:0] out_48,
  output [31:0] out_49,
  output [31:0] out_50,
  output [31:0] out_51,
  output [31:0] out_52,
  output [31:0] out_53,
  output [31:0] out_54,
  output [31:0] out_55,
  output [31:0] out_56,
  output [31:0] out_57,
  output [31:0] out_58,
  output [31:0] out_59,
  output [31:0] out_60,
  output [31:0] out_61,
  output [31:0] out_62,
  output [31:0] out_63,
  output [31:0] out_64,
  output [31:0] out_65,
  output [31:0] out_66,
  output [31:0] out_67,
  output [31:0] out_68,
  output [31:0] out_69
);

  wire _1_prime_prime_prime, _2_prime_prime_prime, _3_prime_prime_prime, _4_prime_prime_prime,
       _11_prime_prime_prime, _12_prime_prime_prime, _13_prime_prime_prime, _14_prime_prime_prime, and_1_out,
       and_3_out, and_4_out, and_5_out, cdm_8_mark5_1_data_inst, cdm_8_mark5_1_mem_cycle, clk_t, clock_1_out,
       clr, collision_1_trigger, comparator_1_eq, comparator_2_gt, comparator_3_eq, comparator_4_lt,
       comparator_5_eq, controlled_buffer_1_out, controlled_buffer_3_out, d_ff_1_q, d_ff_2_q, d_ff_3_q,
       d_ff_4_q, decoder_1_out0, decoder_1_out1, decoder_3_out1, decoder_3_out2, decoder_3_out3,
       decoder_3_out4, DONE, I_O_sel, init, multiplexer_2_out, multiplexer_3_out, not_2_out, not_3_out,
       not_4_out, not_5_out, not_6_out, not_7_out, or_1_out, or_32_out, or_33_out, or_34_out, or_35_out,
       or_36_out, pull_resistor_34_node, pull_resistor_37_node, r, r_w, random_1_out, ready, register_36_q,
       transfer, w, \Частота_сдвигов_out , \Частота_стрельбы_out ;
  wire [1:0] controlled_buffer_2_out, random_2_out, register_1_q;
  wire [2:0] counter_2_q;
  wire [4:0] adder_1_out, counter_1_q, height, inc_5bit_1_r, register_12_q;
  wire [7:0] addr, arr0, arr1, arr2, arr3, cdm_8_mark5_1_data_out, cdm_8_mark5_1_ps, cdm_8_mark5_1_r0,
       cdm_8_mark5_1_r1, cdm_8_mark5_1_r2, cdm_8_mark5_1_r3, cdm_8_mark5_1_sp, controlled_buffer_5_out,
       controlled_buffer_8_out, coord, demultiplexer_3_out4, enem, info, io_data, multiplexer_1_out,
       multiplexer_6_out, Oarr0, Oarr1, Oarr2, Oarr3, Oenem, PC, register_8_q, register_9_q, register_10_q,
       register_11_q, register_20_q, register_21_q, register_22_q, register_23_q, subtractor_1_out;
  wire [31:0] _2e, _2f, _3e, _3f, _4f, _5e, _5f, _6e, _6f, _7e, _7f, _8e, _8f, _9e, _9f, _10e, _10f, _11e,
       _11f, _12e, _12f, _13e, _13f, _14e, _14f, _15e, _15f, _16e, _16f, _17e, _17f, _18e, _18f, _19e, _19f,
       _20e, _20f, _21e, _21f, _22e, _22f, _23e, _23f, _24bul, _24e, _24f, _25e, _25f, _26e, _26f, _27e,
       _27f, _28e, _28f, _29e, _29f, _30e, _30f, _31e, _31f, collision_1_out, demultiplexer_1_out0,
       multiplexer_4_out, multiplexer_5_out, pull_resistor_33_node, register_2_q, register_13_q,
       register_15_q, register_16_q, register_24_q, register_31_q, register_33_q;

  assign controlled_buffer_1_out = initgame ? clock_1_out : 1'bz;  // Controlled_Buffer controlled_buffer_1
  Clock #(.lowDuration(20)) clock_1 (.out(clock_1_out));
  Random #(.width(1)) random_1 (.clk(controlled_buffer_1_out), .out(random_1_out));  // open: next, clr
  CDMEnemShoot cdmenemshoot_1 (
    .\rand (controlled_buffer_2_out), .shift(info), .En(controlled_buffer_1_out), .out(coord),
    .\Частота_процессора (clk_t), .Ready(ready));
  Subtractor subtractor_1 (.a(coord), .b(8'h1), .out(subtractor_1_out));  // open: bin, bout
  D_Flip_Flop d_ff_1 (.Q(d_ff_1_q), .preset(or_1_out), .reset(controlled_buffer_1_out));  // open: clk, D, Qn, en
  or or_1 (or_1_out, transfer, wall);
  Multiplexer #(.width(8), .enable("false")) multiplexer_1 (
    .in0(coord), .in1(subtractor_1_out), .out(multiplexer_1_out), .sel(random_1_out));
  D_Flip_Flop d_ff_2 (.D(ready), .Q(d_ff_2_q), .preset(ready), .reset(d_ff_1_q));  // open: clk, Qn, en
  Demultiplexer #(.select(5), .enable("false")) demultiplexer_1 (
    .out0(demultiplexer_1_out0[0]), .out1(demultiplexer_1_out0[1]), .out2(demultiplexer_1_out0[2]),
    .out3(demultiplexer_1_out0[3]), .out4(demultiplexer_1_out0[4]), .out5(demultiplexer_1_out0[5]),
    .out6(demultiplexer_1_out0[6]), .out7(demultiplexer_1_out0[7]), .out8(demultiplexer_1_out0[8]),
    .out9(demultiplexer_1_out0[9]), .out10(demultiplexer_1_out0[10]), .out11(demultiplexer_1_out0[11]),
    .out12(demultiplexer_1_out0[12]), .out13(demultiplexer_1_out0[13]), .out14(demultiplexer_1_out0[14]),
    .out15(demultiplexer_1_out0[15]), .out16(demultiplexer_1_out0[16]), .out17(demultiplexer_1_out0[17]),
    .out18(demultiplexer_1_out0[18]), .out19(demultiplexer_1_out0[19]), .out20(demultiplexer_1_out0[20]),
    .out21(demultiplexer_1_out0[21]), .out22(demultiplexer_1_out0[22]), .out23(demultiplexer_1_out0[23]),
    .out24(demultiplexer_1_out0[24]), .out25(demultiplexer_1_out0[25]), .out26(demultiplexer_1_out0[26]),
    .out27(demultiplexer_1_out0[27]), .out28(demultiplexer_1_out0[28]), .out29(demultiplexer_1_out0[29]),
    .out30(demultiplexer_1_out0[30]), .out31(demultiplexer_1_out0[31]), .in(d_ff_2_q),
    .sel(multiplexer_1_out[4:0]));
  assign out_37 = _31f | _31e;  // OR_Gate or_2, 32 bits wide
  assign out_39 = _30f | _30e;  // OR_Gate or_3, 32 bits wide
  assign out_42 = _29f | _29e;  // OR_Gate or_4, 32 bits wide
  assign out_45 = _28f | _28e;  // OR_Gate or_5, 32 bits wide
  assign out_47 = _27f | _27e;  // OR_Gate or_6, 32 bits wide
  assign out_50 = _26f | _26e;  // OR_Gate or_7, 32 bits wide
  assign out_53 = _25f | _25e;  // OR_Gate or_8, 32 bits wide
  assign out_56 = _24f | _24e;  // OR_Gate or_9, 32 bits wide
  assign out_59 = _23f | _23e;  // OR_Gate or_10, 32 bits wide
  assign out_62 = _22f | _22e;  // OR_Gate or_11, 32 bits wide
  assign out_65 = _21f | _21e;  // OR_Gate or_12, 32 bits wide
  assign out_68 = _20f | _20e;  // OR_Gate or_13, 32 bits wide
  assign out_36 = _19f | _19e;  // OR_Gate or_14, 32 bits wide
  assign out_38 = _18f | _18e;  // OR_Gate or_15, 32 bits wide
  assign out_41 = _17f | _17e;  // OR_Gate or_16, 32 bits wide
  assign out_44 = _16f | _16e;  // OR_Gate or_17, 32 bits wide
  assign out_46 = _15f | _15e;  // OR_Gate or_18, 32 bits wide
  assign out_49 = _14f | _14e;  // OR_Gate or_19, 32 bits wide
  assign out_52 = _13f | _13e;  // OR_Gate or_20, 32 bits wide
  assign out_55 = _12f | _12e;  // OR_Gate or_21, 32 bits wide
  assign out_58 = _11f | _11e;  // OR_Gate or_22, 32 bits wide
  assign out_61 = _10f | _10e;  // OR_Gate or_23, 32 bits wide
  assign out_64 = _9f | _9e;  // OR_Gate or_24, 32 bits wide
  assign out_67 = _8f | _8e;  // OR_Gate or_25, 32 bits wide
  assign out_69 = _7f | _7e;  // OR_Gate or_26, 32 bits wide
  assign out_66 = _6f | _6e;  // OR_Gate or_27, 32 bits wide
  assign out_63 = _5f | _5e;  // OR_Gate or_28, 32 bits wide
  assign out_60 = _4f | out_43;  // OR_Gate or_29, 32 bits wide
  assign out_57 = _3f | _3e;  // OR_Gate or_30, 32 bits wide
  assign out_54 = _2e | _2f;  // OR_Gate or_31, 32 bits wide
  Register #(.width(2)) register_1 (.D(random_2_out), .Q(register_1_q), .clk(comparator_1_eq));  // open: en, clr
  Random #(.width(2)) random_2 (.clk(controlled_buffer_1_out), .out(random_2_out));  // open: next, clr
  Register #(.width(32)) register_2 (.D(demultiplexer_1_out0), .Q(register_2_q), .clk(d_ff_1_q));  // open: en, clr
  Register register_3 (.D(8'h18), .en(init), .Q(register_13_q[31:24]), .clk(init), .clr(_1_prime_prime_prime));
  assign controlled_buffer_2_out = multiplexer_2_out ? register_1_q : 2'bz;  // Controlled_Buffer controlled_buffer_2
  Counter #(.width(5), .max('h1d)) counter_1 (
    .Q(counter_1_q), .carry(transfer), .clk(\Частота_стрельбы_out ), .clr(d_ff_1_q));  // open: load, D, count
  Clock #(.highDuration(10), .lowDuration(10)) \u_Частота_стрельбы  (.out(\Частота_стрельбы_out ));
  Register register_4 (.D(8'h18), .en(init), .Q(register_15_q[31:24]), .clk(init), .clr(_11_prime_prime_prime));
  Comparator #(.width(5), .mode("unsigned")) comparator_1 (
    .a(counter_1_q), .b({5{1'b0}}), .eq(comparator_1_eq));  // open: gt, lt
  Register register_5 (.D(8'h18), .en(init), .Q(register_13_q[15:8]), .clk(init), .clr(_3_prime_prime_prime));
  Register register_6 (.D(8'h18), .en(init), .Q(register_13_q[23:16]), .clk(init), .clr(_2_prime_prime_prime));
  Register register_7 (.D(8'h18), .en(init), .Q(register_15_q[23:16]), .clk(init), .clr(_12_prime_prime_prime));
  Register register_8 (.D(8'h24), .en(init), .Q(register_8_q), .clk(init), .clr(_4_prime_prime_prime));
  Register register_9 (.D(8'h24), .en(init), .Q(register_9_q), .clk(init), .clr(_3_prime_prime_prime));
  Register register_10 (.D(8'h24), .en(init), .Q(register_10_q), .clk(init), .clr(_2_prime_prime_prime));
  Register register_11 (.D(8'h24), .en(init), .Q(register_11_q), .clk(init), .clr(_1_prime_prime_prime));
  Multiplexer #(.select(2), .enable("false")) multiplexer_2 (
    .in0(Oenem[4]), .in1(Oenem[5]), .in2(Oenem[6]), .in3(Oenem[7]), .out(multiplexer_2_out),
    .sel(register_1_q));
  Adder #(.width(5)) adder_1 (.a(register_12_q), .b(counter_1_q), .out(adder_1_out));  // open: cin, cout
  Register #(.width(5)) register_12 (
    .D(height), .en(comparator_1_eq), .Q(register_12_q), .clk(\Частота_стрельбы_out ));  // open: clr
  Register register_13 (.D(8'h18), .en(init), .Q(register_13_q[7:0]), .clk(init), .clr(_4_prime_prime_prime));
  Register register_14 (.D(8'h18), .en(init), .Q(register_15_q[15:8]), .clk(init), .clr(_13_prime_prime_prime));
  Pull_Resistor pull_resistor_1 (.node(_31f));
  Pull_Resistor pull_resistor_2 (.node(_19f));
  Pull_Resistor pull_resistor_3 (.node(_18f));
  Demultiplexer #(.select(5), .width(32), .tristate("true"), .disabled(0)) demultiplexer_2 (
    .out0(_31f), .out1(_30f), .out2(_29f), .out3(_28f), .out4(_27f), .out5(_26f), .out6(_25f), .out7(_24f),
    .out8(_23f), .out9(_22f), .out10(_21f), .out11(_20f), .out12(_19f), .out13(_18f), .out14(_17f),
    .out15(_16f), .out16(_15f), .out17(_14f), .out18(_13f), .out19(_12f), .out20(_11f), .out21(_10f),
    .out22(_9f), .out23(_8f), .out24(_7f), .out25(_6f), .out26(_5f), .out27(_4f), .out28(_3f), .out29(_2f),
    .out30(out_51), .out31(out_48), .in(register_2_q), .sel(adder_1_out), .en(and_1_out));
  Pull_Resistor pull_resistor_4 (.node(_8f));
  Pull_Resistor pull_resistor_5 (.node(_7f));
  and and_1 (and_1_out, multiplexer_2_out, comparator_2_gt);
  Comparator #(.width(5), .mode("unsigned")) comparator_2 (
    .a(adder_1_out), .b(register_12_q), .gt(comparator_2_gt));  // open: eq, lt
  Register register_15 (.D(8'h18), .en(init), .Q(register_15_q[7:0]), .clk(init), .clr(_14_prime_prime_prime));
  Register register_16 (.D(8'h24), .en(init), .Q(register_16_q[7:0]), .clk(init), .clr(_14_prime_prime_prime));
  Register register_17 (.D(8'h24), .en(init), .Q(register_16_q[15:8]), .clk(init), .clr(_13_prime_prime_prime));
  Register register_18 (.D(8'h24), .en(init), .Q(register_16_q[23:16]), .clk(init), .clr(_12_prime_prime_prime));
  Register register_19 (.D(8'h24), .en(init), .Q(register_16_q[31:24]), .clk(init), .clr(_11_prime_prime_prime));
  Pull_Resistor pull_resistor_6 (.node(_30f));
  Pull_Resistor pull_resistor_7 (.node(_29f));
  Pull_Resistor pull_resistor_8 (.node(_28f));
  Pull_Resistor pull_resistor_9 (.node(_27f));
  Pull_Resistor pull_resistor_10 (.node(_26f));
  Pull_Resistor pull_resistor_11 (.node(_25f));
  Pull_Resistor pull_resistor_12 (.node(_24f));
  Pull_Resistor pull_resistor_13 (.node(_23f));
  Pull_Resistor pull_resistor_14 (.node(_17f));
  Pull_Resistor pull_resistor_15 (.node(_16f));
  Pull_Resistor pull_resistor_16 (.node(_15f));
  Pull_Resistor pull_resistor_17 (.node(_14f));
  Pull_Resistor pull_resistor_18 (.node(_13f));
  Pull_Resistor pull_resistor_19 (.node(_12f));
  Pull_Resistor pull_resistor_20 (.node(_11f));
  Pull_Resistor pull_resistor_21 (.node(_10f));
  Pull_Resistor pull_resistor_22 (.node(_6f));
  Pull_Resistor pull_resistor_23 (.node(_5f));
  Pull_Resistor pull_resistor_24 (.node(_4f));
  Pull_Resistor pull_resistor_25 (.node(_3f));
  Pull_Resistor pull_resistor_26 (.node(_2f));
  Pull_Resistor pull_resistor_27 (.node(out_51));
  Pull_Resistor pull_resistor_28 (.node(out_48));
  Register register_20 (.D(8'h5a), .en(init), .Q(register_20_q), .clk(init), .clr(_14_prime_prime_prime));
  Register register_21 (.D(8'h24), .en(init), .Q(register_21_q), .clk(init), .clr(_13_prime_prime_prime));
  Register register_22 (.D(8'h24), .en(init), .Q(register_22_q), .clk(init), .clr(_12_prime_prime_prime));
  Register register_23 (.D(8'h5a), .en(init), .Q(register_23_q), .clk(init), .clr(_11_prime_prime_prime));
  assign {_1_prime_prime_prime, _2_prime_prime_prime, _3_prime_prime_prime, _4_prime_prime_prime, _11_prime_prime_prime, _12_prime_prime_prime, _13_prime_prime_prime, _14_prime_prime_prime} = ~Oenem;  // NOT_Gate not_1, 8 bits wide
  Pull_Resistor pull_resistor_29 (.node(_22f));
  Pull_Resistor pull_resistor_30 (.node(_21f));
  Pull_Resistor pull_resistor_31 (.node(_20f));
  Pull_Resistor pull_resistor_32 (.node(_9f));
  not not_2 (not_2_out, boom);
  Clock #(.highDuration(180), .lowDuration(180)) \u_Частота_сдвигов  (.out(\Частота_сдвигов_out ));
  Register register_24 (.D(8'h5a), .en(init), .Q(register_24_q[7:0]), .clk(init), .clr(_4_prime_prime_prime));
  Register register_25 (.D(8'h24), .en(init), .Q(register_24_q[15:8]), .clk(init), .clr(_3_prime_prime_prime));
  Register register_26 (.D(8'h24), .en(init), .Q(register_24_q[23:16]), .clk(init), .clr(_2_prime_prime_prime));
  Register register_27 (.D(8'h5a), .en(init), .Q(register_24_q[31:24]), .clk(init), .clr(_1_prime_prime_prime));
  assign controlled_buffer_3_out = not_2_out ? \Частота_сдвигов_out  : 1'bz;  // Controlled_Buffer controlled_buffer_3
  Register register_28 (.D(8'h24), .en(init), .Q(register_31_q[7:0]), .clk(init), .clr(_14_prime_prime_prime));
  Register register_29 (.D(8'h18), .en(init), .Q(register_31_q[15:8]), .clk(init), .clr(_13_prime_prime_prime));
  Register register_30 (.D(8'h18), .en(init), .Q(register_31_q[23:16]), .clk(init), .clr(_12_prime_prime_prime));
  Register register_31 (.D(8'h24), .en(init), .Q(register_31_q[31:24]), .clk(init), .clr(_11_prime_prime_prime));
  and and_2 (I_O_sel, and_4_out, decoder_1_out1);
  Clock \u_Частота_процессора  (.out(clk_t));
  and and_3 (and_3_out, boom, ~not_3_out, initgame);  // AND_Gate
  Register register_32 (.D(8'h24), .en(init), .Q(register_33_q[7:0]), .clk(init), .clr(_4_prime_prime_prime));
  Register register_33 (.D(8'h18), .en(init), .Q(register_33_q[15:8]), .clk(init), .clr(_3_prime_prime_prime));
  Register register_34 (.D(8'h18), .en(init), .Q(register_33_q[23:16]), .clk(init), .clr(_2_prime_prime_prime));
  Register register_35 (.D(8'h24), .en(init), .Q(register_33_q[31:24]), .clk(init), .clr(_1_prime_prime_prime));
  Pull_Resistor pull_resistor_33 (.node(pull_resistor_33_node));
  Shifts shifts_1 (
    .\Выход_2 (_2e), .\Вход_0 (register_33_q), .out_16(_3e), .in_2(register_24_q), .out_20(out_43),
    .in_3(register_13_q), .out_24(_5e), .in_4({register_11_q, register_10_q, register_9_q, register_8_q}),
    .out_28(_6e), .in_5(pull_resistor_33_node), .out_32(_7e), .in_6(register_31_q), .out_36(_8e),
    .in_7({register_23_q, register_22_q, register_21_q, register_20_q}), .out_39(_9e), .in_8(register_15_q),
    .out_13(_10e), .in_9(register_16_q), .out_17(_11e), .clock(controlled_buffer_3_out), .out_25(_13e),
    .\Очистка__когда_0 (initgame), .out_29(_14e), .info(info), .out_33(_15e), .height(height), .out_37(_16e),
    .out_40(_17e), .out_14(_18e), .out_18(_19e), .out_22(_20e), .out_26(_21e), .out_30(_22e), .out_34(_23e),
    .out_38(_24e), .out_41(_25e), .out_15(_26e), .out_19(_27e), .out_23(_28e), .out_27(_29e), .out_31(_30e),
    .out_35(_31e), .out_21(_12e));
  and and_4 (and_4_out, addr[4], addr[5], addr[6], addr[7], decoder_1_out1);
  // Probe on cdm_8_mark5_1_r1
  // Probe on cdm_8_mark5_1_r3
  // Probe on PC
  // Probe on cdm_8_mark5_1_r0
  // Probe on cdm_8_mark5_1_r2
  Multiplexer #(.enable("false")) multiplexer_3 (.in0(1'b0), .in1(clk_t), .out(multiplexer_3_out), .sel(not_3_out));
  not not_3 (not_3_out, d_ff_3_q);
  D_Flip_Flop #(.trigger("falling")) d_ff_3 (
    .Q(d_ff_3_q), .preset(comparator_3_eq), .reset(d_ff_4_q));  // open: clk, D, Qn, en
  Comparator comparator_3 (.a(PC), .b(8'h8), .eq(comparator_3_eq));  // open: gt, lt
  D_Flip_Flop #(.trigger("falling")) d_ff_4 (.clk(clk_t), .D(and_3_out), .Q(d_ff_4_q));  // open: Qn, preset, en, reset
  and and_5 (and_5_out, decoder_1_out1, ~and_4_out);  // AND_Gate
  // Probe on cdm_8_mark5_1_ps
  // Probe on cdm_8_mark5_1_sp
  CdM_8_mark5 cdm_8_mark5_1 (
    .clock(multiplexer_3_out), .addr(addr), .mem_read(r_w), .mem_cycle(cdm_8_mark5_1_mem_cycle),
    .data_inst(cdm_8_mark5_1_data_inst), .data_out(cdm_8_mark5_1_data_out),
    .data_in(controlled_buffer_5_out), .r0(cdm_8_mark5_1_r0), .r1(cdm_8_mark5_1_r1), .r2(cdm_8_mark5_1_r2),
    .r3(cdm_8_mark5_1_r3), .PC(PC), .SP(cdm_8_mark5_1_sp), .PS(cdm_8_mark5_1_ps));  // open: IAck, IRQ, vec, reset
  Register #(.width(1)) register_36 (.D(pull_resistor_34_node), .Q(register_36_q), .clk(clk));  // open: en, clr
  Decoder #(.disabled(0)) decoder_1 (
    .out0(decoder_1_out0), .out1(decoder_1_out1), .sel(cdm_8_mark5_1_data_inst), .en(cdm_8_mark5_1_mem_cycle));
  not not_4 (not_4_out, r_w);
  assign io_data = not_4_out ? cdm_8_mark5_1_data_out : 8'bz;  // Controlled_Buffer controlled_buffer_4
  assign controlled_buffer_5_out = r_w ? io_data : 8'bz;  // Controlled_Buffer controlled_buffer_5
  D_Flip_Flop d_ff_5 (.clk(register_36_q), .D(register_36_q), .Q(boom), .reset(DONE));  // open: Qn, preset, en
  Pull_Resistor pull_resistor_34 (.node(pull_resistor_34_node));
  Register #(.width(32)) register_37 (
    .D(collision_1_out), .en(pull_resistor_34_node), .Q({arr3, arr2, arr1, arr0}), .clk(clk));  // open: clr
  // Probe on addr
  not not_5 (not_5_out, boom);
  assign init = not_5_out ? clk_t : 1'bz;  // Controlled_Buffer controlled_buffer_6
  Collision collision_1 (
    .OUT(collision_1_out), .A(multiplexer_4_out), .B(multiplexer_5_out), .Trigger(collision_1_trigger));
  Comparator #(.width(5), .mode("unsigned")) comparator_4 (
    .a(5'b00011), .b(inc_5bit_1_r), .lt(comparator_4_lt));  // open: gt, eq
  assign pull_resistor_34_node = comparator_4_lt ? collision_1_trigger : 1'bz;  // Controlled_Buffer controlled_buffer_7
  // Probe on io_data
  RAM ram_1 (.addr(addr), .data(io_data), .sel(and_5_out), .clk(clk_t), .ld(r_w), .clr(clr));
  ROM rom_1 (.addr(addr), .data(io_data), .sel(decoder_1_out0));
  Multiplexer #(.select(5), .width(32), .enable("false")) multiplexer_4 (
    .in0({32{1'b0}}), .in1({32{1'b0}}), .in2(in_17), .in3(in_20), .in4(in_23), .in5(in_26), .in6(in_29),
    .in7(in_32), .in8(in_33), .in9(in_30), .in10(in_27), .in11(in_24), .in12(in_21), .in13(in_18),
    .in14(in_14), .in15(in_12), .in16(in_10), .in17(in_8), .in18(in_6), .in19(in_3), .in20(in_34),
    .in21(in_31), .in22(in_28), .in23(in_25), .in24(_24bul), .in25(in_19), .in26(in_15), .in27(in_13),
    .in28(in_11), .in29(in_9), .in30(in_7), .in31(in_4), .out(multiplexer_4_out), .sel(Num));
  Inc_5bit inc_5bit_1 (.X(Num), .R(inc_5bit_1_r));  // open: Cout
  Multiplexer #(.select(5), .width(32), .enable("false")) multiplexer_5 (
    .in0({32{1'b0}}), .in1({32{1'b0}}), .in2(_2e), .in3(_3e), .in4(out_43), .in5(_5e), .in6(_6e), .in7(_7e),
    .in8(_8e), .in9(_9e), .in10(_10e), .in11(_11e), .in12(_12e), .in13(_13e), .in14(_14e), .in15(_15e),
    .in16(_16e), .in17(_17e), .in18(_18e), .in19(_19e), .in20(_20e), .in21(_21e), .in22(_22e), .in23(_23e),
    .in24(_24e), .in25(_25e), .in26(_26e), .in27(_27e), .in28(_28e), .in29(_29e), .in30(_30e), .in31(_31e),
    .out(multiplexer_5_out), .sel(inc_5bit_1_r));
  Decoder decoder_2 (.out0(r), .out1(w), .sel(r_w), .en(I_O_sel));
  Pull_Resistor pull_resistor_35 (.node(r));
  or or_32 (or_32_out, r, w);
  Pull_Resistor pull_resistor_36 (.node(w));
  Pull_Resistor pull_resistor_37 (.node(pull_resistor_37_node));
  Decoder #(.select(4)) decoder_3 (
    .out0(pull_resistor_37_node), .out1(decoder_3_out1), .out2(decoder_3_out2), .out3(decoder_3_out3),
    .out4(decoder_3_out4), .sel(addr[3:0]), .en(or_32_out));  // open: out5, out6, out7, out8, out9, out10, out11, out12, out13, out14, out15
  Pull_Resistor pull_resistor_38 (.node(decoder_3_out3));
  assign controlled_buffer_8_out = r ? io_data : 8'bz;  // Controlled_Buffer controlled_buffer_8
  Demultiplexer #(.select(4), .width(8)) demultiplexer_3 (
    .out4(demultiplexer_3_out4), .in(controlled_buffer_8_out), .sel(addr[3:0]), .en(r));  // open: out0, out1, out2, out3, out5, out6, out7, out8, out9, out10, out11, out12, out13, out14, out15
  Pull_Resistor pull_resistor_39 (.node(decoder_3_out1));
  Pull_Resistor pull_resistor_40 (.node(decoder_3_out2));
  Pull_Resistor pull_resistor_41 (.node(decoder_3_out4));
  assign enem = r ? demultiplexer_3_out4 : 8'bz;  // Controlled_Buffer controlled_buffer_9
  assign io_data = w ? multiplexer_6_out : 8'bz;  // Controlled_Buffer controlled_buffer_10
  Multiplexer #(.select(4), .width(8)) multiplexer_6 (
    .in0(Oarr0), .in1(Oarr1), .in2(Oarr2), .in3(Oarr3), .in4(Oenem), .out(multiplexer_6_out),
    .sel(addr[3:0]), .en(w));  // open: in5, in6, in7, in8, in9, in10, in11, in12, in13, in14, in15
  or or_33 (or_33_out, pull_resistor_37_node, boom);
  or or_34 (or_34_out, decoder_3_out1, boom);
  or or_35 (or_35_out, decoder_3_out2, boom);
  or or_36 (or_36_out, decoder_3_out3, boom);
  Counter #(.width(3), .max('h2)) counter_2 (
    .count(decoder_3_out4), .Q(counter_2_q), .clk(decoder_3_out4), .clr(not_6_out));  // open: load, D, carry
  not not_6 (not_6_out, boom);
  nor nor_1 (win, Oenem[0], Oenem[1], Oenem[2], Oenem[3], Oenem[4], Oenem[5], Oenem[6], Oenem[7]);
  Register register_38 (.D(arr0), .en(or_33_out), .Q(Oarr0), .clk(clk_t));  // open: clr
  Register register_39 (.D(arr1), .en(or_34_out), .Q(Oarr1), .clk(clk_t));  // open: clr
  Register register_40 (.D(arr2), .en(or_35_out), .Q(Oarr2), .clk(clk_t));  // open: clr
  Register register_41 (.D(arr3), .en(or_36_out), .Q(Oarr3), .clk(clk_t));  // open: clr
  Register register_42 (.D(enem), .en(decoder_3_out4), .Q(Oenem), .clk(clk_t));  // open: clr
  Comparator #(.width(3), .mode("unsigned")) comparator_5 (
    .a(counter_2_q), .b(3'b010), .eq(comparator_5_eq));  // open: gt, lt
  Register #(.width(1)) register_43 (
    .D(comparator_5_eq), .Q(DONE), .clk(comparator_5_eq), .clr(not_7_out));  // open: en
  not not_7 (not_7_out, boom);

  // Other names for the same wires on the sheet: _0[31:0] = out_48; _0f[31:0] = out_48; _1[31:0] = out_51;
  //   _1f[31:0] = out_51; _2[31:0] = out_54; _2bul[31:0] = in_17; _3[31:0] = out_57; _3bul[31:0] = in_20;
  //   _4[31:0] = out_60; _4bul[31:0] = in_23; _4e[31:0] = out_43; _5[31:0] = out_63; _5bul[31:0] = in_26;
  //   _6[31:0] = out_66; _6bul[31:0] = in_29; _7[31:0] = out_69; _7bul[31:0] = in_32; _8[31:0] = out_67;
  //   _8bul[31:0] = in_33; _9[31:0] = out_64; _9bul[31:0] = in_30; _10[31:0] = out_61; _10bul[31:0] = in_27;
  //   _11[31:0] = out_58; _11bul[31:0] = in_24; _12[31:0] = out_55; _12bul[31:0] = in_21; _13[31:0] = out_52;
  //   _13bul[31:0] = in_18; _14[31:0] = out_49; _14bul[31:0] = in_14; _15[31:0] = out_46; _15bul[31:0] = in_12;
  //   _16[31:0] = out_44; _16bul[31:0] = in_10; _17[31:0] = out_41; _17bul[31:0] = in_8; _18[31:0] = out_38;
  //   _18bul[31:0] = in_6; _19[31:0] = out_36; _19bul[31:0] = in_3; _20[31:0] = out_68; _20bul[31:0] = in_34;
  //   _21[31:0] = out_65; _21bul[31:0] = in_31; _22[31:0] = out_62; _22bul[31:0] = in_28; _23[31:0] = out_59;
  //   _23bul[31:0] = in_25; _24[31:0] = out_56; _25[31:0] = out_53; _25bul[31:0] = in_19; _26[31:0] = out_50;
  //   _26bul[31:0] = in_15; _27[31:0] = out_47; _27bul[31:0] = in_13; _28[31:0] = out_45; _28bul[31:0] = in_11;
  //   _29[31:0] = out_42; _29bul[31:0] = in_9; _30[31:0] = out_39; _30bul[31:0] = in_7; _31[31:0] = out_37;
  //   _31bul[31:0] = in_4; IOaddr[3:0] = addr[3:0]; gen = clk; res = wall; StartGame = initgame

  // Notes on the sheet:
  //   Enemy shooting
  //   rand
  //   is enemy alive
  //   Collision check
  //   Сохранение строки для кода
  //   contents of rom_1 (hex, n*v repeats v):
  //   c0 c4 c0 d1 ff d2 f4 a9 c4 d1 f0 d0 0 d2 3 7 a eb 1e bd 5 e0 19 ee 1e 8f 8c 8a ee 10 d1 1 d2 f4 ba 0
  //   e0 2a 25 88 ee 23 7 4b f e1 38 d0 4 0 e0 38 25 88 ee 31 66 d0 f4 a2 a e0 41 d6 8 d6 1 173*0 1 0 0 4
  //   ff
  //   запись в регитсры (st)
  //   чтение из регитров (ld)
  //   is processing of collision finished
  //   bullet in processing
endmodule
module Shifts (
  input  [31:0] \Вход_0 ,
  input  [31:0] in_2,
  input  [31:0] in_3,
  input  [31:0] in_4,
  input  [31:0] in_5,
  input  [31:0] in_6,
  input  [31:0] in_7,
  input  [31:0] in_8,
  input  [31:0] in_9,
  input  clock,
  input  \Очистка__когда_0 ,
  output [31:0] \Выход_2 ,
  output [31:0] out_13,
  output [31:0] out_14,
  output [31:0] out_15,
  output [31:0] out_16,
  output [31:0] out_17,
  output [31:0] out_18,
  output [31:0] out_19,
  output [31:0] out_20,
  output [31:0] out_21,
  output [31:0] out_22,
  output [31:0] out_23,
  output [31:0] out_24,
  output [31:0] out_25,
  output [31:0] out_26,
  output [31:0] out_27,
  output [31:0] out_28,
  output [31:0] out_29,
  output [31:0] out_30,
  output [31:0] out_31,
  output [31:0] out_32,
  output [31:0] out_33,
  output [31:0] out_34,
  output [31:0] out_35,
  output [31:0] out_36,
  output [31:0] out_37,
  output [31:0] out_38,
  output [31:0] out_39,
  output [31:0] out_40,
  output [31:0] out_41,
  output [7:0] info,
  output [4:0] height
);

  wire comparator_1_eq, comparator_2_eq, comparator_3_eq, comparator_4_eq, comparator_5_eq, comparator_6_eq,
       L, nor_1_out, or_1_out, or_2_out, or_3_out, R, START;
  wire [2:0] counter_1_q;
  wire [4:0] counter_2_q;
  wire [7:0] adder_1_out;
  wire [31:0] controlled_buffer_1_out, controlled_buffer_2_out, controlled_buffer_3_out,
       controlled_buffer_4_out, controlled_buffer_5_out, controlled_buffer_6_out, controlled_buffer_7_out,
       controlled_buffer_8_out, controlled_buffer_9_out, pull_resistor_2_node, shifterright_1_out_11,
       shifterright_1_out_12, shifterright_1_out_13, shifterright_1_out_14, shifterright_1_out_15,
       shifterright_1_out_16, shifterright_1_out_17, shifterright_1_out_18, shifterright_1_out_19,
       shifterright_2_out_11, shifterright_2_out_12, shifterright_2_out_13, shifterright_2_out_14,
       shifterright_2_out_15, shifterright_2_out_16, shifterright_2_out_17, shifterright_2_out_18,
       shifterright_2_out_19;

  Adder adder_1 (.a({{7{1'b0}}, R}), .b({8{1'b0}}), .out(adder_1_out));  // open: cin, cout
  Counter #(.width(3), .max('h5)) counter_1 (.Q(counter_1_q), .clk(clock), .clr(START));  // open: load, D, count, carry
  Subtractor subtractor_1 (.a(adder_1_out), .b({{7{1'b0}}, L}), .out(info));  // open: bin, bout
  Comparator #(.width(3)) comparator_1 (.a(counter_1_q), .b(3'b010), .eq(comparator_1_eq));  // open: gt, lt
  Comparator #(.width(3)) comparator_2 (.a(counter_1_q), .b(3'b101), .eq(comparator_2_eq));  // open: gt, lt
  Comparator #(.width(3)) comparator_3 (.a(counter_1_q), .b(3'b001), .eq(comparator_3_eq));  // open: gt, lt
  Comparator #(.width(3)) comparator_4 (.a(counter_1_q), .b(3'b011), .eq(comparator_4_eq));  // open: gt, lt
  Comparator #(.width(3)) comparator_5 (.a(counter_1_q), .b(3'b100), .eq(comparator_5_eq));  // open: gt, lt
  Comparator #(.width(3)) comparator_6 (.a(counter_1_q), .b(3'b000), .eq(comparator_6_eq));  // open: gt, lt
  Counter #(.width(5), .max('h1f)) counter_2 (
    .Q(counter_2_q), .clk(or_1_out), .clr(START));  // open: load, D, count, carry
  or or_1 (or_1_out, comparator_1_eq, comparator_2_eq);
  Counter #(.width(1), .max('h1)) counter_3 (.Q(L), .clk(or_2_out), .clr(START));  // open: load, D, count, carry
  or or_2 (or_2_out, comparator_3_eq, comparator_4_eq);
  Counter #(.width(1), .max('h1)) counter_4 (.Q(R), .clk(or_3_out), .clr(START));  // open: load, D, count, carry
  or or_3 (or_3_out, comparator_5_eq, comparator_6_eq);
  Adder #(.width(5)) adder_2 (.a(5'b00011), .b(counter_2_q), .out(height));  // open: cin, cout
  not not_1 (START, \Очистка__когда_0 );
  Pull_Resistor pull_resistor_1 (.node(\Очистка__когда_0 ));
  Pull_Resistor pull_resistor_2 (.node(pull_resistor_2_node));
  assign controlled_buffer_1_out = nor_1_out ? \Вход_0  : 32'bz;  // Controlled_Buffer controlled_buffer_1
  assign controlled_buffer_2_out = nor_1_out ? in_2 : 32'bz;  // Controlled_Buffer controlled_buffer_2
  assign controlled_buffer_3_out = nor_1_out ? in_3 : 32'bz;  // Controlled_Buffer controlled_buffer_3
  assign controlled_buffer_4_out = nor_1_out ? in_4 : 32'bz;  // Controlled_Buffer controlled_buffer_4
  assign controlled_buffer_5_out = nor_1_out ? in_5 : 32'bz;  // Controlled_Buffer controlled_buffer_5
  assign controlled_buffer_6_out = nor_1_out ? in_6 : 32'bz;  // Controlled_Buffer controlled_buffer_6
  assign controlled_buffer_7_out = nor_1_out ? in_7 : 32'bz;  // Controlled_Buffer controlled_buffer_7
  assign controlled_buffer_8_out = nor_1_out ? in_8 : 32'bz;  // Controlled_Buffer controlled_buffer_8
  assign controlled_buffer_9_out = nor_1_out ? in_9 : 32'bz;  // Controlled_Buffer controlled_buffer_9
  nor nor_1 (nor_1_out, L, R);
  ShifterRight shifterright_1 (
    .\Вход_0 (\Вход_0 ), .out_11(shifterright_1_out_11), .in_2(in_2), .out_12(shifterright_1_out_12),
    .in_3(in_3), .out_13(shifterright_1_out_13), .in_4(in_4), .out_14(shifterright_1_out_14), .in_5(in_5),
    .out_15(shifterright_1_out_15), .in_6(in_6), .out_16(shifterright_1_out_16), .in_7(in_7),
    .out_17(shifterright_1_out_17), .in_8(in_8), .out_18(shifterright_1_out_18), .in_9(in_9),
    .out_19(shifterright_1_out_19), .in_10(R));
  assign controlled_buffer_1_out = R ? shifterright_1_out_11 : 32'bz;  // Controlled_Buffer controlled_buffer_10
  assign controlled_buffer_2_out = R ? shifterright_1_out_12 : 32'bz;  // Controlled_Buffer controlled_buffer_11
  assign controlled_buffer_3_out = R ? shifterright_1_out_13 : 32'bz;  // Controlled_Buffer controlled_buffer_12
  assign controlled_buffer_4_out = R ? shifterright_1_out_14 : 32'bz;  // Controlled_Buffer controlled_buffer_13
  assign controlled_buffer_5_out = R ? shifterright_1_out_15 : 32'bz;  // Controlled_Buffer controlled_buffer_14
  assign controlled_buffer_6_out = R ? shifterright_1_out_16 : 32'bz;  // Controlled_Buffer controlled_buffer_15
  assign controlled_buffer_7_out = R ? shifterright_1_out_17 : 32'bz;  // Controlled_Buffer controlled_buffer_16
  assign controlled_buffer_8_out = R ? shifterright_1_out_18 : 32'bz;  // Controlled_Buffer controlled_buffer_17
  assign controlled_buffer_9_out = R ? shifterright_1_out_19 : 32'bz;  // Controlled_Buffer controlled_buffer_18
  ShifterRight shifterright_2 (
    .\Вход_0 (\Вход_0 ), .out_11(shifterright_2_out_11), .in_2(in_2), .out_12(shifterright_2_out_12),
    .in_3(in_3), .out_13(shifterright_2_out_13), .in_4(in_4), .out_14(shifterright_2_out_14), .in_5(in_5),
    .out_15(shifterright_2_out_15), .in_6(in_6), .out_16(shifterright_2_out_16), .in_7(in_7),
    .out_17(shifterright_2_out_17), .in_8(in_8), .out_18(shifterright_2_out_18), .in_9(in_9),
    .out_19(shifterright_2_out_19), .in_10(L));
  assign controlled_buffer_1_out = L ? shifterright_2_out_11 : 32'bz;  // Controlled_Buffer controlled_buffer_19
  assign controlled_buffer_2_out = L ? shifterright_2_out_12 : 32'bz;  // Controlled_Buffer controlled_buffer_20
  assign controlled_buffer_3_out = L ? shifterright_2_out_13 : 32'bz;  // Controlled_Buffer controlled_buffer_21
  assign controlled_buffer_4_out = L ? shifterright_2_out_14 : 32'bz;  // Controlled_Buffer controlled_buffer_22
  assign controlled_buffer_5_out = L ? shifterright_2_out_15 : 32'bz;  // Controlled_Buffer controlled_buffer_23
  assign controlled_buffer_6_out = L ? shifterright_2_out_16 : 32'bz;  // Controlled_Buffer controlled_buffer_24
  assign controlled_buffer_7_out = L ? shifterright_2_out_17 : 32'bz;  // Controlled_Buffer controlled_buffer_25
  assign controlled_buffer_8_out = L ? shifterright_2_out_18 : 32'bz;  // Controlled_Buffer controlled_buffer_26
  assign controlled_buffer_9_out = L ? shifterright_2_out_19 : 32'bz;  // Controlled_Buffer controlled_buffer_27
  ShifterDown shifterdown_1 (
    .\Вход_0 (controlled_buffer_1_out), .\Выход_0 (out_35), .in_3(controlled_buffer_2_out), .out_37(out_31),
    .in_5(controlled_buffer_3_out), .out_39(out_27), .in_7(controlled_buffer_4_out), .out_41(out_23),
    .in_10(controlled_buffer_5_out), .out_43(out_19), .in_9(counter_2_q), .En(\Очистка__когда_0 ),
    .in_13(controlled_buffer_6_out), .out_45(out_15), .in_15(controlled_buffer_7_out), .out_47(out_41),
    .in_17(controlled_buffer_8_out), .out_49(out_38), .in_19(controlled_buffer_9_out), .out_51(out_34),
    .in_21(pull_resistor_2_node), .out_53(out_30), .in_23(pull_resistor_2_node), .out_55(out_26),
    .in_25(pull_resistor_2_node), .out_57(out_22), .in_27(pull_resistor_2_node), .out_59(out_18),
    .in_29(pull_resistor_2_node), .out_61(out_14), .in_31(pull_resistor_2_node), .out_63(out_40),
    .in_33(pull_resistor_2_node), .out_64(out_37), .in_2(pull_resistor_2_node), .out_36(out_33),
    .in_4(pull_resistor_2_node), .out_38(out_29), .in_6(pull_resistor_2_node), .out_40(out_25),
    .in_8(pull_resistor_2_node), .out_42(out_21), .in_11(pull_resistor_2_node), .out_44(out_17),
    .in_14(pull_resistor_2_node), .out_46(out_13), .in_16(pull_resistor_2_node), .out_48(out_39),
    .in_18(pull_resistor_2_node), .out_50(out_36), .in_20(pull_resistor_2_node), .out_52(out_32),
    .in_22(pull_resistor_2_node), .out_54(out_28), .in_24(pull_resistor_2_node), .out_56(out_24),
    .in_26(pull_resistor_2_node), .out_58(out_20), .in_28(pull_resistor_2_node), .out_60(out_16),
    .in_30(pull_resistor_2_node), .out_62(\Выход_2 ), .in_32(pull_resistor_2_node),
    .in_34(pull_resistor_2_node));

  // Other names for the same wires on the sheet: _2e[31:0] = \Выход_2 ; _3e[31:0] = out_16; _4e[31:0] = out_20;
  //   _5e[31:0] = out_24; _6e[31:0] = out_28; _7e[31:0] = out_32; _8e[31:0] = out_36; _9e[31:0] = out_39;
  //   _10e[31:0] = out_13; _11e[31:0] = out_17; _12e[31:0] = out_21; _13e[31:0] = out_25; _14e[31:0] = out_29;
  //   _15e[31:0] = out_33; _16e[31:0] = out_37; _17e[31:0] = out_40; _18e[31:0] = out_14; _19e[31:0] = out_18;
  //   _20e[31:0] = out_22; _21e[31:0] = out_26; _22e[31:0] = out_30; _23e[31:0] = out_34; _24e[31:0] = out_38;
  //   _25e[31:0] = out_41; _26e[31:0] = out_15; _27e[31:0] = out_19; _28e[31:0] = out_23; _29e[31:0] = out_27;
  //   _30e[31:0] = out_31; _31e[31:0] = out_35; En = \Очистка__когда_0 ; Heght[4:0] = height

  // Notes on the sheet:
  //   V
  //   >
  //   <
endmodule

module ShifterDown (
  input  [31:0] \Вход_0 ,
  input  [31:0] in_2,
  input  [31:0] in_3,
  input  [31:0] in_4,
  input  [31:0] in_5,
  input  [31:0] in_6,
  input  [31:0] in_7,
  input  [31:0] in_8,
  input  [4:0] in_9,
  input  [31:0] in_10,
  input  [31:0] in_11,
  input  En,
  input  [31:0] in_13,
  input  [31:0] in_14,
  input  [31:0] in_15,
  input  [31:0] in_16,
  input  [31:0] in_17,
  input  [31:0] in_18,
  input  [31:0] in_19,
  input  [31:0] in_20,
  input  [31:0] in_21,
  input  [31:0] in_22,
  input  [31:0] in_23,
  input  [31:0] in_24,
  input  [31:0] in_25,
  input  [31:0] in_26,
  input  [31:0] in_27,
  input  [31:0] in_28,
  input  [31:0] in_29,
  input  [31:0] in_30,
  input  [31:0] in_31,
  input  [31:0] in_32,
  input  [31:0] in_33,
  input  [31:0] in_34,
  output [31:0] \Выход_0 ,
  output [31:0] out_36,
  output [31:0] out_37,
  output [31:0] out_38,
  output [31:0] out_39,
  output [31:0] out_40,
  output [31:0] out_41,
  output [31:0] out_42,
  output [31:0] out_43,
  output [31:0] out_44,
  output [31:0] out_45,
  output [31:0] out_46,
  output [31:0] out_47,
  output [31:0] out_48,
  output [31:0] out_49,
  output [31:0] out_50,
  output [31:0] out_51,
  output [31:0] out_52,
  output [31:0] out_53,
  output [31:0] out_54,
  output [31:0] out_55,
  output [31:0] out_56,
  output [31:0] out_57,
  output [31:0] out_58,
  output [31:0] out_59,
  output [31:0] out_60,
  output [31:0] out_61,
  output [31:0] out_62,
  output [31:0] out_63,
  output [31:0] out_64
);

  wire not_1_out;
  wire [4:0] controlled_buffer_1_out, inc_5bit_1_r, inc_5bit_2_r, inc_5bit_3_r, inc_5bit_4_r, inc_5bit_5_r,
       inc_5bit_6_r, inc_5bit_7_r, inc_5bit_8_r, inc_5bit_9_r, inc_5bit_10_r, inc_5bit_11_r, inc_5bit_12_r,
       inc_5bit_13_r, inc_5bit_14_r, inc_5bit_15_r, inc_5bit_16_r, inc_5bit_17_r, inc_5bit_18_r,
       inc_5bit_19_r, inc_5bit_20_r, inc_5bit_21_r, inc_5bit_22_r, inc_5bit_23_r, inc_5bit_24_r,
       inc_5bit_25_r, inc_5bit_26_r, inc_5bit_27_r, inc_5bit_28_r, inc_5bit_29_r;
  wire [31:0] _30_prime, _31_prime;

  Pull_Resistor pull_resistor_1 (.node(\Выход_0 ));
  Pull_Resistor pull_resistor_2 (.node(out_37));
  Pull_Resistor pull_resistor_3 (.node(out_39));
  Pull_Resistor pull_resistor_4 (.node(out_41));
  Pull_Resistor pull_resistor_5 (.node(out_43));
  Pull_Resistor pull_resistor_6 (.node(out_45));
  Pull_Resistor pull_resistor_7 (.node(out_47));
  Pull_Resistor pull_resistor_8 (.node(out_49));
  Pull_Resistor pull_resistor_9 (.node(out_51));
  Pull_Resistor pull_resistor_10 (.node(out_53));
  Pull_Resistor pull_resistor_11 (.node(out_55));
  Pull_Resistor pull_resistor_12 (.node(out_57));
  Pull_Resistor pull_resistor_13 (.node(out_59));
  Pull_Resistor pull_resistor_14 (.node(out_61));
  Pull_Resistor pull_resistor_15 (.node(out_63));
  Pull_Resistor pull_resistor_16 (.node(out_64));
  Pull_Resistor pull_resistor_17 (.node(out_36));
  Pull_Resistor pull_resistor_18 (.node(out_38));
  Pull_Resistor pull_resistor_19 (.node(out_40));
  Pull_Resistor pull_resistor_20 (.node(out_42));
  Pull_Resistor pull_resistor_21 (.node(out_44));
  Pull_Resistor pull_resistor_22 (.node(out_46));
  Pull_Resistor pull_resistor_23 (.node(out_48));
  Pull_Resistor pull_resistor_24 (.node(out_50));
  Pull_Resistor pull_resistor_25 (.node(out_52));
  Pull_Resistor pull_resistor_26 (.node(out_54));
  Pull_Resistor pull_resistor_27 (.node(out_56));
  Pull_Resistor pull_resistor_28 (.node(out_58));
  Pull_Resistor pull_resistor_29 (.node(out_60));
  Pull_Resistor pull_resistor_30 (.node(out_62));
  assign controlled_buffer_1_out = En ? in_9 : 5'bz;  // Controlled_Buffer controlled_buffer_1
  not not_1 (not_1_out, En);
  assign controlled_buffer_1_out = not_1_out ? {5{1'b0}} : 5'bz;  // Controlled_Buffer controlled_buffer_2
  Demultiplexer #(.select(5), .width(32), .tristate("true"), .enable("false")) demultiplexer_1 (
    .out0(\Выход_0 ), .out1(out_37), .out2(out_39), .out3(out_41), .out4(out_43), .out5(out_45),
    .out6(out_47), .out7(out_49), .out8(out_51), .out9(out_53), .out10(out_55), .out11(out_57),
    .out12(out_59), .out13(out_61), .out14(out_63), .out15(out_64), .out16(out_36), .out17(out_38),
    .out18(out_40), .out19(out_42), .out20(out_44), .out21(out_46), .out22(out_48), .out23(out_50),
    .out24(out_52), .out25(out_54), .out26(out_56), .out27(out_58), .out28(out_60), .out29(out_62),
    .out30(_30_prime), .out31(_31_prime), .in(\Вход_0 ), .sel(controlled_buffer_1_out));
  Demultiplexer #(.select(5), .width(32), .tristate("true"), .enable("false")) demultiplexer_2 (
    .out4(out_43), .out5(out_45), .out6(out_47), .out7(out_49), .out8(out_51), .out9(out_53), .out10(out_55),
    .out11(out_57), .out12(out_59), .out13(out_61), .out14(out_63), .out15(out_64), .out16(out_36),
    .out17(out_38), .out18(out_40), .out19(out_42), .out20(out_44), .out21(out_46), .out22(out_48),
    .out23(out_50), .out24(out_52), .out25(out_54), .out26(out_56), .out27(out_58), .out28(out_60),
    .out29(out_62), .out30(_30_prime), .out31(_31_prime), .in(in_10), .sel(inc_5bit_1_r));  // open: out0, out1, out2, out3
  Inc_5bit inc_5bit_1 (.X(inc_5bit_12_r), .R(inc_5bit_1_r));  // open: Cout
  Demultiplexer #(.select(5), .width(32), .tristate("true"), .enable("false")) demultiplexer_3 (
    .out8(out_51), .out9(out_53), .out10(out_55), .out11(out_57), .out12(out_59), .out13(out_61),
    .out14(out_63), .out15(out_64), .out16(out_36), .out17(out_38), .out18(out_40), .out19(out_42),
    .out20(out_44), .out21(out_46), .out22(out_48), .out23(out_50), .out24(out_52), .out25(out_54),
    .out26(out_56), .out27(out_58), .out28(out_60), .out29(out_62), .out30(_30_prime), .out31(_31_prime),
    .in(in_19), .sel(inc_5bit_2_r));  // open: out0, out1, out2, out3, out4, out5, out6, out7
  Inc_5bit inc_5bit_2 (.X(inc_5bit_13_r), .R(inc_5bit_2_r));  // open: Cout
  Demultiplexer #(.select(5), .width(32), .tristate("true"), .enable("false")) demultiplexer_4 (
    .out12(out_59), .out13(out_61), .out14(out_63), .out15(out_64), .out16(out_36), .out17(out_38),
    .out18(out_40), .out19(out_42), .out20(out_44), .out21(out_46), .out22(out_48), .out23(out_50),
    .out24(out_52), .out25(out_54), .out26(out_56), .out27(out_58), .out28(out_60), .out29(out_62),
    .out30(_30_prime), .out31(_31_prime), .in(in_27), .sel(inc_5bit_3_r));  // open: out0, out1, out2, out3, out4, out5, out6, out7, out8, out9, out10, out11
  Inc_5bit inc_5bit_3 (.X(inc_5bit_14_r), .R(inc_5bit_3_r));  // open: Cout
  Inc_5bit inc_5bit_4 (.X(controlled_buffer_1_out), .R(inc_5bit_4_r));  // open: Cout
  Inc_5bit inc_5bit_5 (.X(inc_5bit_1_r), .R(inc_5bit_5_r));  // open: Cout
  Inc_5bit inc_5bit_6 (.X(inc_5bit_2_r), .R(inc_5bit_6_r));  // open: Cout
  Inc_5bit inc_5bit_7 (.X(inc_5bit_3_r), .R(inc_5bit_7_r));  // open: Cout
  Demultiplexer #(.select(5), .width(32), .tristate("true"), .enable("false")) demultiplexer_5 (
    .out1(out_37), .out2(out_39), .out3(out_41), .out4(out_43), .out5(out_45), .out6(out_47), .out7(out_49),
    .out8(out_51), .out9(out_53), .out10(out_55), .out11(out_57), .out12(out_59), .out13(out_61),
    .out14(out_63), .out15(out_64), .out16(out_36), .out17(out_38), .out18(out_40), .out19(out_42),
    .out20(out_44), .out21(out_46), .out22(out_48), .out23(out_50), .out24(out_52), .out25(out_54),
    .out26(out_56), .out27(out_58), .out28(out_60), .out29(out_62), .out30(_30_prime), .out31(_31_prime),
    .in(in_3), .sel(inc_5bit_4_r));  // open: out0
  Demultiplexer #(.select(5), .width(32), .tristate("true"), .enable("false")) demultiplexer_6 (
    .out5(out_45), .out6(out_47), .out7(out_49), .out8(out_51), .out9(out_53), .out10(out_55),
    .out11(out_57), .out12(out_59), .out13(out_61), .out14(out_63), .out15(out_64), .out16(out_36),
    .out17(out_38), .out18(out_40), .out19(out_42), .out20(out_44), .out21(out_46), .out22(out_48),
    .out23(out_50), .out24(out_52), .out25(out_54), .out26(out_56), .out27(out_58), .out28(out_60),
    .out29(out_62), .out30(_30_prime), .out31(_31_prime), .in(in_13), .sel(inc_5bit_5_r));  // open: out0, out1, out2, out3, out4
  Demultiplexer #(.select(5), .width(32), .tristate("true"), .enable("false")) demultiplexer_7 (
    .out9(out_53), .out10(out_55), .out11(out_57), .out12(out_59), .out13(out_61), .out14(out_63),
    .out15(out_64), .out16(out_36), .out17(out_38), .out18(out_40), .out19(out_42), .out20(out_44),
    .out21(out_46), .out22(out_48), .out23(out_50), .out24(out_52), .out25(out_54), .out26(out_56),
    .out27(out_58), .out28(out_60), .out29(out_62), .out30(_30_prime), .out31(_31_prime), .in(in_21),
    .sel(inc_5bit_6_r));  // open: out0, out1, out2, out3, out4, out5, out6, out7, out8
  Demultiplexer #(.select(5), .width(32), .tristate("true"), .enable("false")) demultiplexer_8 (
    .out13(out_61), .out14(out_63), .out15(out_64), .out16(out_36), .out17(out_38), .out18(out_40),
    .out19(out_42), .out20(out_44), .out21(out_46), .out22(out_48), .out23(out_50), .out24(out_52),
    .out25(out_54), .out26(out_56), .out27(out_58), .out28(out_60), .out29(out_62), .out30(_30_prime),
    .out31(_31_prime), .in(in_29), .sel(inc_5bit_7_r));  // open: out0, out1, out2, out3, out4, out5, out6, out7, out8, out9, out10, out11, out12
  Inc_5bit inc_5bit_8 (.X(inc_5bit_4_r), .R(inc_5bit_8_r));  // open: Cout
  Demultiplexer #(.select(5), .width(32), .tristate("true"), .enable("false")) demultiplexer_9 (
    .out6(out_47), .out7(out_49), .out8(out_51), .out9(out_53), .out10(out_55), .out11(out_57),
    .out12(out_59), .out13(out_61), .out14(out_63), .out15(out_64), .out16(out_36), .out17(out_38),
    .out18(out_40), .out19(out_42), .out20(out_44), .out21(out_46), .out22(out_48), .out23(out_50),
    .out24(out_52), .out25(out_54), .out26(out_56), .out27(out_58), .out28(out_60), .out29(out_62),
    .out30(_30_prime), .out31(_31_prime), .in(in_15), .sel(inc_5bit_9_r));  // open: out0, out1, out2, out3, out4, out5
  Inc_5bit inc_5bit_9 (.X(inc_5bit_5_r), .R(inc_5bit_9_r));  // open: Cout
  Demultiplexer #(.select(5), .width(32), .tristate("true"), .enable("false")) demultiplexer_10 (
    .out10(out_55), .out11(out_57), .out12(out_59), .out13(out_61), .out14(out_63), .out15(out_64),
    .out16(out_36), .out17(out_38), .out18(out_40), .out19(out_42), .out20(out_44), .out21(out_46),
    .out22(out_48), .out23(out_50), .out24(out_52), .out25(out_54), .out26(out_56), .out27(out_58),
    .out28(out_60), .out29(out_62), .out30(_30_prime), .out31(_31_prime), .in(in_23), .sel(inc_5bit_10_r));  // open: out0, out1, out2, out3, out4, out5, out6, out7, out8, out9
  Inc_5bit inc_5bit_10 (.X(inc_5bit_6_r), .R(inc_5bit_10_r));  // open: Cout
  Demultiplexer #(.select(5), .width(32), .tristate("true"), .enable("false")) demultiplexer_11 (
    .out14(out_63), .out15(out_64), .out16(out_36), .out17(out_38), .out18(out_40), .out19(out_42),
    .out20(out_44), .out21(out_46), .out22(out_48), .out23(out_50), .out24(out_52), .out25(out_54),
    .out26(out_56), .out27(out_58), .out28(out_60), .out29(out_62), .out30(_30_prime), .out31(_31_prime),
    .in(in_31), .sel(inc_5bit_11_r));  // open: out0, out1, out2, out3, out4, out5, out6, out7, out8, out9, out10, out11, out12, out13
  Inc_5bit inc_5bit_11 (.X(inc_5bit_7_r), .R(inc_5bit_11_r));  // open: Cout
  Demultiplexer #(.select(5), .width(32), .tristate("true"), .enable("false")) demultiplexer_12 (
    .out2(out_39), .out3(out_41), .out4(out_43), .out5(out_45), .out6(out_47), .out7(out_49), .out8(out_51),
    .out9(out_53), .out10(out_55), .out11(out_57), .out12(out_59), .out13(out_61), .out14(out_63),
    .out15(out_64), .out16(out_36), .out17(out_38), .out18(out_40), .out19(out_42), .out20(out_44),
    .out21(out_46), .out22(out_48), .out23(out_50), .out24(out_52), .out25(out_54), .out26(out_56),
    .out27(out_58), .out28(out_60), .out29(out_62), .out30(_30_prime), .out31(_31_prime), .in(in_5),
    .sel(inc_5bit_8_r));  // open: out0, out1
  Demultiplexer #(.select(5), .width(32), .tristate("true"), .enable("false")) demultiplexer_13 (
    .out3(out_41), .out4(out_43), .out5(out_45), .out6(out_47), .out7(out_49), .out8(out_51), .out9(out_53),
    .out10(out_55), .out11(out_57), .out12(out_59), .out13(out_61), .out14(out_63), .out15(out_64),
    .out16(out_36), .out17(out_38), .out18(out_40), .out19(out_42), .out20(out_44), .out21(out_46),
    .out22(out_48), .out23(out_50), .out24(out_52), .out25(out_54), .out26(out_56), .out27(out_58),
    .out28(out_60), .out29(out_62), .out30(_30_prime), .out31(_31_prime), .in(in_7), .sel(inc_5bit_12_r));  // open: out0, out1, out2
  Inc_5bit inc_5bit_12 (.X(inc_5bit_8_r), .R(inc_5bit_12_r));  // open: Cout
  Demultiplexer #(.select(5), .width(32), .tristate("true"), .enable("false")) demultiplexer_14 (
    .out7(out_49), .out8(out_51), .out9(out_53), .out10(out_55), .out11(out_57), .out12(out_59),
    .out13(out_61), .out14(out_63), .out15(out_64), .out16(out_36), .out17(out_38), .out18(out_40),
    .out19(out_42), .out20(out_44), .out21(out_46), .out22(out_48), .out23(out_50), .out24(out_52),
    .out25(out_54), .out26(out_56), .out27(out_58), .out28(out_60), .out29(out_62), .out30(_30_prime),
    .out31(_31_prime), .in(in_17), .sel(inc_5bit_13_r));  // open: out0, out1, out2, out3, out4, out5, out6
  Inc_5bit inc_5bit_13 (.X(inc_5bit_9_r), .R(inc_5bit_13_r));  // open: Cout
  Demultiplexer #(.select(5), .width(32), .tristate("true"), .enable("false")) demultiplexer_15 (
    .out11(out_57), .out12(out_59), .out13(out_61), .out14(out_63), .out15(out_64), .out16(out_36),
    .out17(out_38), .out18(out_40), .out19(out_42), .out20(out_44), .out21(out_46), .out22(out_48),
    .out23(out_50), .out24(out_52), .out25(out_54), .out26(out_56), .out27(out_58), .out28(out_60),
    .out29(out_62), .out30(_30_prime), .out31(_31_prime), .in(in_25), .sel(inc_5bit_14_r));  // open: out0, out1, out2, out3, out4, out5, out6, out7, out8, out9, out10
  Inc_5bit inc_5bit_14 (.X(inc_5bit_10_r), .R(inc_5bit_14_r));  // open: Cout
  Demultiplexer #(.select(5), .width(32), .tristate("true"), .enable("false")) demultiplexer_16 (
    .out15(out_64), .out16(out_36), .out17(out_38), .out18(out_40), .out19(out_42), .out20(out_44),
    .out21(out_46), .out22(out_48), .out23(out_50), .out24(out_52), .out25(out_54), .out26(out_56),
    .out27(out_58), .out28(out_60), .out29(out_62), .out30(_30_prime), .out31(_31_prime), .in(in_33),
    .sel(inc_5bit_15_r));  // open: out0, out1, out2, out3, out4, out5, out6, out7, out8, out9, out10, out11, out12, out13, out14
  Inc_5bit inc_5bit_15 (.X(inc_5bit_11_r), .R(inc_5bit_15_r));  // open: Cout
  Demultiplexer #(.select(5), .width(32), .tristate("true"), .enable("false")) demultiplexer_17 (
    .out16(out_36), .out17(out_38), .out18(out_40), .out19(out_42), .out20(out_44), .out21(out_46),
    .out22(out_48), .out23(out_50), .out24(out_52), .out25(out_54), .out26(out_56), .out27(out_58),
    .out28(out_60), .out29(out_62), .out30(_30_prime), .out31(_31_prime), .in(in_2), .sel(inc_5bit_16_r));  // open: out0, out1, out2, out3, out4, out5, out6, out7, out8, out9, out10, out11, out12, out13, out14, out15
  Inc_5bit inc_5bit_16 (.X(inc_5bit_15_r), .R(inc_5bit_16_r));  // open: Cout
  Demultiplexer #(.select(5), .width(32), .tristate("true"), .enable("false")) demultiplexer_18 (
    .out20(out_44), .out21(out_46), .out22(out_48), .out23(out_50), .out24(out_52), .out25(out_54),
    .out26(out_56), .out27(out_58), .out28(out_60), .out29(out_62), .out30(_30_prime), .out31(_31_prime),
    .in(in_11), .sel(inc_5bit_17_r));  // open: out0, out1, out2, out3, out4, out5, out6, out7, out8, out9, out10, out11, out12, out13, out14, out15, out16, out17, out18, out19
  Inc_5bit inc_5bit_17 (.X(inc_5bit_27_r), .R(inc_5bit_17_r));  // open: Cout
  Demultiplexer #(.select(5), .width(32), .tristate("true"), .enable("false")) demultiplexer_19 (
    .out24(out_52), .out25(out_54), .out26(out_56), .out27(out_58), .out28(out_60), .out29(out_62),
    .out30(_30_prime), .out31(_31_prime), .in(in_20), .sel(inc_5bit_18_r));  // open: out0, out1, out2, out3, out4, out5, out6, out7, out8, out9, out10, out11, out12, out13, out14, out15, out16, out17, out18, out19, out20, out21, out22, out23
  Inc_5bit inc_5bit_18 (.X(inc_5bit_28_r), .R(inc_5bit_18_r));  // open: Cout
  Demultiplexer #(.select(5), .width(32), .tristate("true"), .enable("false")) demultiplexer_20 (
    .out28(out_60), .out29(out_62), .out30(_30_prime), .out31(_31_prime), .in(in_28), .sel(inc_5bit_19_r));  // open: out0, out1, out2, out3, out4, out5, out6, out7, out8, out9, out10, out11, out12, out13, out14, out15, out16, out17, out18, out19, out20, out21, out22, out23, out24, out25, out26, out27
  Inc_5bit inc_5bit_19 (.X(inc_5bit_29_r), .R(inc_5bit_19_r));  // open: Cout
  Inc_5bit inc_5bit_20 (.X(inc_5bit_16_r), .R(inc_5bit_20_r));  // open: Cout
  Inc_5bit inc_5bit_21 (.X(inc_5bit_17_r), .R(inc_5bit_21_r));  // open: Cout
  Inc_5bit inc_5bit_22 (.X(inc_5bit_18_r), .R(inc_5bit_22_r));  // open: Cout
  Inc_5bit inc_5bit_23 (.X(inc_5bit_19_r), .R(inc_5bit_23_r));  // open: Cout
  Demultiplexer #(.select(5), .width(32), .tristate("true"), .enable("false")) demultiplexer_21 (
    .out17(out_38), .out18(out_40), .out19(out_42), .out20(out_44), .out21(out_46), .out22(out_48),
    .out23(out_50), .out24(out_52), .out25(out_54), .out26(out_56), .out27(out_58), .out28(out_60),
    .out29(out_62), .out30(_30_prime), .out31(_31_prime), .in(in_4), .sel(inc_5bit_20_r));  // open: out0, out1, out2, out3, out4, out5, out6, out7, out8, out9, out10, out11, out12, out13, out14, out15, out16
  Demultiplexer #(.select(5), .width(32), .tristate("true"), .enable("false")) demultiplexer_22 (
    .out21(out_46), .out22(out_48), .out23(out_50), .out24(out_52), .out25(out_54), .out26(out_56),
    .out27(out_58), .out28(out_60), .out29(out_62), .out30(_30_prime), .out31(_31_prime), .in(in_14),
    .sel(inc_5bit_21_r));  // open: out0, out1, out2, out3, out4, out5, out6, out7, out8, out9, out10, out11, out12, out13, out14, out15, out16, out17, out18, out19, out20
  Demultiplexer #(.select(5), .width(32), .tristate("true"), .enable("false")) demultiplexer_23 (
    .out25(out_54), .out26(out_56), .out27(out_58), .out28(out_60), .out29(out_62), .out30(_30_prime),
    .out31(_31_prime), .in(in_22), .sel(inc_5bit_22_r));  // open: out0, out1, out2, out3, out4, out5, out6, out7, out8, out9, out10, out11, out12, out13, out14, out15, out16, out17, out18, out19, out20, out21, out22, out23, out24
  Demultiplexer #(.select(5), .width(32), .tristate("true"), .enable("false")) demultiplexer_24 (
    .out29(out_62), .out30(_30_prime), .out31(_31_prime), .in(in_30), .sel(inc_5bit_23_r));  // open: out0, out1, out2, out3, out4, out5, out6, out7, out8, out9, out10, out11, out12, out13, out14, out15, out16, out17, out18, out19, out20, out21, out22, out23, out24, out25, out26, out27, out28
  Demultiplexer #(.select(5), .width(32), .tristate("true"), .enable("false")) demultiplexer_25 (
    .out18(out_40), .out19(out_42), .out20(out_44), .out21(out_46), .out22(out_48), .out23(out_50),
    .out24(out_52), .out25(out_54), .out26(out_56), .out27(out_58), .out28(out_60), .out29(out_62),
    .out30(_30_prime), .out31(_31_prime), .in(in_6), .sel(inc_5bit_24_r));  // open: out0, out1, out2, out3, out4, out5, out6, out7, out8, out9, out10, out11, out12, out13, out14, out15, out16, out17
  Inc_5bit inc_5bit_24 (.X(inc_5bit_20_r), .R(inc_5bit_24_r));  // open: Cout
  Demultiplexer #(.select(5), .width(32), .tristate("true"), .enable("false")) demultiplexer_26 (
    .out22(out_48), .out23(out_50), .out24(out_52), .out25(out_54), .out26(out_56), .out27(out_58),
    .out28(out_60), .out29(out_62), .out30(_30_prime), .out31(_31_prime), .in(in_16), .sel(inc_5bit_25_r));  // open: out0, out1, out2, out3, out4, out5, out6, out7, out8, out9, out10, out11, out12, out13, out14, out15, out16, out17, out18, out19, out20, out21
  Inc_5bit inc_5bit_25 (.X(inc_5bit_21_r), .R(inc_5bit_25_r));  // open: Cout
  Demultiplexer #(.select(5), .width(32), .tristate("true"), .enable("false")) demultiplexer_27 (
    .out26(out_56), .out27(out_58), .out28(out_60), .out29(out_62), .out30(_30_prime), .out31(_31_prime),
    .in(in_24), .sel(inc_5bit_26_r));  // open: out0, out1, out2, out3, out4, out5, out6, out7, out8, out9, out10, out11, out12, out13, out14, out15, out16, out17, out18, out19, out20, out21, out22, out23, out24, out25
  Inc_5bit inc_5bit_26 (.X(inc_5bit_22_r), .R(inc_5bit_26_r));  // open: Cout
  Demultiplexer #(.select(5), .width(32), .tristate("true"), .enable("false")) demultiplexer_28 (
    .out19(out_42), .out20(out_44), .out21(out_46), .out22(out_48), .out23(out_50), .out24(out_52),
    .out25(out_54), .out26(out_56), .out27(out_58), .out28(out_60), .out29(out_62), .out30(_30_prime),
    .out31(_31_prime), .in(in_8), .sel(inc_5bit_27_r));  // open: out0, out1, out2, out3, out4, out5, out6, out7, out8, out9, out10, out11, out12, out13, out14, out15, out16, out17, out18
  Inc_5bit inc_5bit_27 (.X(inc_5bit_24_r), .R(inc_5bit_27_r));  // open: Cout
  Demultiplexer #(.select(5), .width(32), .tristate("true"), .enable("false")) demultiplexer_29 (
    .out23(out_50), .out24(out_52), .out25(out_54), .out26(out_56), .out27(out_58), .out28(out_60),
    .out29(out_62), .out30(_30_prime), .out31(_31_prime), .in(in_18), .sel(inc_5bit_28_r));  // open: out0, out1, out2, out3, out4, out5, out6, out7, out8, out9, out10, out11, out12, out13, out14, out15, out16, out17, out18, out19, out20, out21, out22
  Inc_5bit inc_5bit_28 (.X(inc_5bit_25_r), .R(inc_5bit_28_r));  // open: Cout
  Demultiplexer #(.select(5), .width(32), .tristate("true"), .enable("false")) demultiplexer_30 (
    .out27(out_58), .out28(out_60), .out29(out_62), .out30(_30_prime), .out31(_31_prime), .in(in_26),
    .sel(inc_5bit_29_r));  // open: out0, out1, out2, out3, out4, out5, out6, out7, out8, out9, out10, out11, out12, out13, out14, out15, out16, out17, out18, out19, out20, out21, out22, out23, out24, out25, out26
  Inc_5bit inc_5bit_29 (.X(inc_5bit_26_r), .R(inc_5bit_29_r));  // open: Cout

  // Other names for the same wires on the sheet: _0[31:0] = \Вход_0 ; _0_prime[31:0] = \Выход_0 ; _1[31:0] = in_3;
  //   _1_prime[31:0] = out_37; _2[31:0] = in_5; _2_prime[31:0] = out_39; _3[31:0] = in_7; _3_prime[31:0] = out_41;
  //   _4[31:0] = in_10; _4_prime[31:0] = out_43; _5[31:0] = in_13; _5_prime[31:0] = out_45; _6[31:0] = in_15;
  //   _6_prime[31:0] = out_47; _7[31:0] = in_17; _7_prime[31:0] = out_49; _8[31:0] = in_19; _8_prime[31:0] = out_51;
  //   _9[31:0] = in_21; _9_prime[31:0] = out_53; _10[31:0] = in_23; _10_prime[31:0] = out_55; _11[31:0] = in_25;
  //   _11_prime[31:0] = out_57; _12[31:0] = in_27; _12_prime[31:0] = out_59; _13[31:0] = in_29;
  //   _13_prime[31:0] = out_61; _14[31:0] = in_31; _14_prime[31:0] = out_63; _15[31:0] = in_33;
  //   _15_prime[31:0] = out_64; _16[31:0] = in_2; _16_prime[31:0] = out_36; _17[31:0] = in_4;
  //   _17_prime[31:0] = out_38; _18[31:0] = in_6; _18_prime[31:0] = out_40; _19[31:0] = in_8;
  //   _19_prime[31:0] = out_42; _20[31:0] = in_11; _20_prime[31:0] = out_44; _21[31:0] = in_14;
  //   _21_prime[31:0] = out_46; _22[31:0] = in_16; _22_prime[31:0] = out_48; _23[31:0] = in_18;
  //   _23_prime[31:0] = out_50; _24[31:0] = in_20; _24_prime[31:0] = out_52; _25[31:0] = in_22;
  //   _25_prime[31:0] = out_54; _26[31:0] = in_24; _26_prime[31:0] = out_56; _27[31:0] = in_26;
  //   _27_prime[31:0] = out_58; _28[31:0] = in_28; _28_prime[31:0] = out_60; _29[31:0] = in_30;
  //   _29_prime[31:0] = out_62; _30[31:0] = in_32; _31[31:0] = in_34
endmodule

module ShifterLeft (
  input  [31:0] \Вход_0 ,
  input  [31:0] in_2,
  input  [31:0] in_3,
  input  [31:0] in_4,
  input  [31:0] in_5,
  input  [31:0] in_6,
  input  [31:0] in_7,
  input  [31:0] in_8,
  input  [31:0] in_9,
  input  in_10,
  output [31:0] out_11,
  output [31:0] out_12,
  output [31:0] out_13,
  output [31:0] out_14,
  output [31:0] out_15,
  output [31:0] out_16,
  output [31:0] out_17,
  output [31:0] out_18,
  output [31:0] out_19
);

  wire [4:4] pull_resistor_1_node;
  wire [31:0] shifter_1_out, shifter_2_out, shifter_3_out, shifter_4_out, shifter_5_out, shifter_6_out,
       shifter_7_out, shifter_8_out, shifter_9_out;

  Pull_Resistor pull_resistor_1 (.node(pull_resistor_1_node[4]));
  Shifter #(.width(32)) shifter_1 (.in(\Вход_0 ), .\dist ({{4{pull_resistor_1_node[4]}}, in_10}), .out(shifter_1_out));
  Shifter #(.width(32)) shifter_2 (.in(in_2), .\dist ({{4{pull_resistor_1_node[4]}}, in_10}), .out(shifter_2_out));
  Shifter #(.width(32)) shifter_3 (.in(in_3), .\dist ({{4{pull_resistor_1_node[4]}}, in_10}), .out(shifter_3_out));
  Shifter #(.width(32)) shifter_4 (.in(in_4), .\dist ({{4{pull_resistor_1_node[4]}}, in_10}), .out(shifter_4_out));
  Shifter #(.width(32)) shifter_5 (.in(in_5), .\dist ({{4{pull_resistor_1_node[4]}}, in_10}), .out(shifter_5_out));
  Shifter #(.width(32)) shifter_6 (.in(in_6), .\dist ({{4{pull_resistor_1_node[4]}}, in_10}), .out(shifter_6_out));
  Shifter #(.width(32)) shifter_7 (.in(in_7), .\dist ({{4{pull_resistor_1_node[4]}}, in_10}), .out(shifter_7_out));
  Shifter #(.width(32)) shifter_8 (.in(in_8), .\dist ({{4{pull_resistor_1_node[4]}}, in_10}), .out(shifter_8_out));
  Shifter #(.width(32)) shifter_9 (.in(in_9), .\dist ({{4{pull_resistor_1_node[4]}}, in_10}), .out(shifter_9_out));
  assign out_11 = in_10 ? shifter_1_out : 32'bz;  // Controlled_Buffer controlled_buffer_1
  assign out_12 = in_10 ? shifter_2_out : 32'bz;  // Controlled_Buffer controlled_buffer_2
  assign out_13 = in_10 ? shifter_3_out : 32'bz;  // Controlled_Buffer controlled_buffer_3
  assign out_14 = in_10 ? shifter_4_out : 32'bz;  // Controlled_Buffer controlled_buffer_4
  assign out_15 = in_10 ? shifter_5_out : 32'bz;  // Controlled_Buffer controlled_buffer_5
  assign out_16 = in_10 ? shifter_6_out : 32'bz;  // Controlled_Buffer controlled_buffer_6
  assign out_17 = in_10 ? shifter_7_out : 32'bz;  // Controlled_Buffer controlled_buffer_7
  assign out_18 = in_10 ? shifter_8_out : 32'bz;  // Controlled_Buffer controlled_buffer_8
  assign out_19 = in_10 ? shifter_9_out : 32'bz;  // Controlled_Buffer controlled_buffer_9

  // Other names for the same wires on the sheet: On = in_10
endmodule

module ShifterRight (
  input  [31:0] \Вход_0 ,
  input  [31:0] in_2,
  input  [31:0] in_3,
  input  [31:0] in_4,
  input  [31:0] in_5,
  input  [31:0] in_6,
  input  [31:0] in_7,
  input  [31:0] in_8,
  input  [31:0] in_9,
  input  in_10,
  output [31:0] out_11,
  output [31:0] out_12,
  output [31:0] out_13,
  output [31:0] out_14,
  output [31:0] out_15,
  output [31:0] out_16,
  output [31:0] out_17,
  output [31:0] out_18,
  output [31:0] out_19
);

  wire [4:4] pull_resistor_1_node;
  wire [31:0] shifter_1_out, shifter_2_out, shifter_3_out, shifter_4_out, shifter_5_out, shifter_6_out,
       shifter_7_out, shifter_8_out, shifter_9_out;

  Pull_Resistor pull_resistor_1 (.node(pull_resistor_1_node[4]));
  Shifter #(.width(32), .shift("lr")) shifter_1 (
    .in(\Вход_0 ), .\dist ({{4{pull_resistor_1_node[4]}}, in_10}), .out(shifter_1_out));
  Shifter #(.width(32), .shift("lr")) shifter_2 (
    .in(in_2), .\dist ({{4{pull_resistor_1_node[4]}}, in_10}), .out(shifter_2_out));
  Shifter #(.width(32), .shift("lr")) shifter_3 (
    .in(in_3), .\dist ({{4{pull_resistor_1_node[4]}}, in_10}), .out(shifter_3_out));
  Shifter #(.width(32), .shift("lr")) shifter_4 (
    .in(in_4), .\dist ({{4{pull_resistor_1_node[4]}}, in_10}), .out(shifter_4_out));
  Shifter #(.width(32), .shift("lr")) shifter_5 (
    .in(in_5), .\dist ({{4{pull_resistor_1_node[4]}}, in_10}), .out(shifter_5_out));
  Shifter #(.width(32), .shift("lr")) shifter_6 (
    .in(in_6), .\dist ({{4{pull_resistor_1_node[4]}}, in_10}), .out(shifter_6_out));
  Shifter #(.width(32), .shift("lr")) shifter_7 (
    .in(in_7), .\dist ({{4{pull_resistor_1_node[4]}}, in_10}), .out(shifter_7_out));
  Shifter #(.width(32), .shift("lr")) shifter_8 (
    .in(in_8), .\dist ({{4{pull_resistor_1_node[4]}}, in_10}), .out(shifter_8_out));
  Shifter #(.width(32), .shift("lr")) shifter_9 (
    .in(in_9), .\dist ({{4{pull_resistor_1_node[4]}}, in_10}), .out(shifter_9_out));
  assign out_11 = in_10 ? shifter_1_out : 32'bz;  // Controlled_Buffer controlled_buffer_1
  assign out_12 = in_10 ? shifter_2_out : 32'bz;  // Controlled_Buffer controlled_buffer_2
  assign out_13 = in_10 ? shifter_3_out : 32'bz;  // Controlled_Buffer controlled_buffer_3
  assign out_14 = in_10 ? shifter_4_out : 32'bz;  // Controlled_Buffer controlled_buffer_4
  assign out_15 = in_10 ? shifter_5_out : 32'bz;  // Controlled_Buffer controlled_buffer_5
  assign out_16 = in_10 ? shifter_6_out : 32'bz;  // Controlled_Buffer controlled_buffer_6
  assign out_17 = in_10 ? shifter_7_out : 32'bz;  // Controlled_Buffer controlled_buffer_7
  assign out_18 = in_10 ? shifter_8_out : 32'bz;  // Controlled_Buffer controlled_buffer_8
  assign out_19 = in_10 ? shifter_9_out : 32'bz;  // Controlled_Buffer controlled_buffer_9

  // Other names for the same wires on the sheet: On = in_10
endmodule

module CDMEnemShoot (
  input  [1:0] \rand ,
  input  [7:0] shift,
  input  \Частота_процессора ,
  input  En,
  output [7:0] out,
  output Ready
);

  wire and_2_out, and_3_out, and_4_out, cdm_8_mark5_1_data_inst, cdm_8_mark5_1_mem_cycle, clr, d_ff_1_q,
       d_ff_2_q, decoder_1_out0, decoder_1_out1, decoder_3_out1, decoder_3_out2, I_O_sel, not_1_out,
       not_2_out, or_1_out, pull_resistor_1_node, pull_resistor_4_node, r, r_w, w;
  wire [7:0] addr, cdm_8_mark5_1_data_out, cdm_8_mark5_1_ps, cdm_8_mark5_1_r0, cdm_8_mark5_1_r1,
       cdm_8_mark5_1_r2, cdm_8_mark5_1_r3, cdm_8_mark5_1_sp, controlled_buffer_2_out,
       controlled_buffer_3_out, demultiplexer_1_out2, io_data, multiplexer_2_out, PC, reg0, reg1, res;

  and and_1 (I_O_sel, and_3_out, decoder_1_out1);
  Comparator comparator_1 (.a(PC), .b(8'h1), .eq(Ready));  // open: gt, lt
  D_Flip_Flop #(.trigger("falling")) d_ff_1 (
    .clk(\Частота_процессора ), .D(and_2_out), .Q(d_ff_1_q));  // open: Qn, preset, en, reset
  and and_2 (and_2_out, En, ~not_1_out);  // AND_Gate
  and and_3 (and_3_out, addr[4], addr[5], addr[6], addr[7], decoder_1_out1);
  // Probe on cdm_8_mark5_1_r3
  // Probe on cdm_8_mark5_1_r1
  // Probe on cdm_8_mark5_1_r2
  // Probe on cdm_8_mark5_1_r0
  Pull_Resistor pull_resistor_1 (.node(pull_resistor_1_node));
  Multiplexer #(.enable("false")) multiplexer_1 (
    .in0(1'b0), .in1(\Частота_процессора ), .out(pull_resistor_1_node), .sel(not_1_out));
  D_Flip_Flop #(.trigger("falling")) d_ff_2 (.Q(d_ff_2_q), .preset(Ready), .reset(d_ff_1_q));  // open: clk, D, Qn, en
  and and_4 (and_4_out, decoder_1_out1, ~and_3_out);  // AND_Gate
  // Probe on PC
  // Probe on cdm_8_mark5_1_sp
  // Probe on cdm_8_mark5_1_ps
  CdM_8_mark5 cdm_8_mark5_1 (
    .clock(pull_resistor_1_node), .addr(addr), .mem_read(r_w), .mem_cycle(cdm_8_mark5_1_mem_cycle),
    .data_inst(cdm_8_mark5_1_data_inst), .data_out(cdm_8_mark5_1_data_out),
    .data_in(controlled_buffer_2_out), .r0(cdm_8_mark5_1_r0), .r1(cdm_8_mark5_1_r1), .r2(cdm_8_mark5_1_r2),
    .r3(cdm_8_mark5_1_r3), .PC(PC), .SP(cdm_8_mark5_1_sp), .PS(cdm_8_mark5_1_ps));  // open: IAck, IRQ, vec, reset
  not not_1 (not_1_out, d_ff_2_q);
  Decoder #(.disabled(0)) decoder_1 (
    .out0(decoder_1_out0), .out1(decoder_1_out1), .sel(cdm_8_mark5_1_data_inst), .en(cdm_8_mark5_1_mem_cycle));
  not not_2 (not_2_out, r_w);
  assign io_data = not_2_out ? cdm_8_mark5_1_data_out : 8'bz;  // Controlled_Buffer controlled_buffer_1
  assign controlled_buffer_2_out = r_w ? io_data : 8'bz;  // Controlled_Buffer controlled_buffer_2
  // Probe on addr
  // Probe on io_data
  RAM ram_1 (.addr(addr), .data(io_data), .sel(and_4_out), .clk(\Частота_процессора ), .ld(r_w), .clr(clr));
  ROM rom_1 (.addr(addr), .data(io_data), .sel(decoder_1_out0));
  Decoder decoder_2 (.out0(r), .out1(w), .sel(r_w), .en(I_O_sel));
  Pull_Resistor pull_resistor_2 (.node(r));
  Pull_Resistor pull_resistor_3 (.node(w));
  or or_1 (or_1_out, r, w);
  Pull_Resistor pull_resistor_4 (.node(pull_resistor_4_node));
  Decoder #(.select(4)) decoder_3 (
    .out0(pull_resistor_4_node), .out1(decoder_3_out1), .out2(decoder_3_out2), .sel(addr[3:0]), .en(or_1_out));  // open: out3, out4, out5, out6, out7, out8, out9, out10, out11, out12, out13, out14, out15
  Pull_Resistor pull_resistor_5 (.node(decoder_3_out1));
  assign controlled_buffer_3_out = r ? io_data : 8'bz;  // Controlled_Buffer controlled_buffer_3
  Demultiplexer #(.select(4), .width(8)) demultiplexer_1 (
    .out2(demultiplexer_1_out2), .in(controlled_buffer_3_out), .sel(addr[3:0]), .en(r));  // open: out0, out1, out3, out4, out5, out6, out7, out8, out9, out10, out11, out12, out13, out14, out15
  Pull_Resistor pull_resistor_6 (.node(decoder_3_out2));
  assign res = r ? demultiplexer_1_out2 : 8'bz;  // Controlled_Buffer controlled_buffer_4
  assign io_data = w ? multiplexer_2_out : 8'bz;  // Controlled_Buffer controlled_buffer_5
  Multiplexer #(.select(4), .width(8)) multiplexer_2 (
    .in0(reg0), .in1(reg1), .out(multiplexer_2_out), .sel(addr[3:0]), .en(w));  // open: in2, in3, in4, in5, in6, in7, in8, in9, in10, in11, in12, in13, in14, in15
  Register register_1 (
    .D({{6{1'b0}}, \rand }), .en(pull_resistor_4_node), .Q(reg0), .clk(\Частота_процессора ));  // open: clr
  Register register_2 (.D(shift), .en(decoder_3_out1), .Q(reg1), .clk(\Частота_процессора ));  // open: clr
  Register register_3 (.D(res), .en(decoder_3_out2), .Q(out), .clk(\Частота_процессора ));  // open: clr

  // Other names for the same wires on the sheet: IOaddr[3:0] = addr[3:0]; clk = \Частота_процессора ;
  //   rand_t[1:0] = \rand 

  // Notes on the sheet:
  //   contents of rom_1 (hex, n*v repeats v):
  //   c0 c4 d2 f0 d0 8 d1 0 ba a e0 10 11 8a ee 9 d0 f1 b0 11 d0 4 14 d2 f2 a8 d6 1 213*0 1
  //   запись в регитсры (st)
  //   чтение из регитров (ld)
endmodule
